// Logisim project Compteur.circ as structural Verilog: 1 circuit, main circuit main
module main (
  input  Input_1,
  input  Input_2,
  input  Input_3,
  output [3:0] Output_bus_1
);

  wire d_ff_1_qn, d_ff_2_qn, d_ff_3_qn, d_ff_4_qn, or_1_out;

  D_Flip_Flop d_ff_1 (
    .D(d_ff_1_qn), .clk(Input_1), .Q(Output_bus_1[0]), .Qn(d_ff_1_qn), .reset(or_1_out));  // open: preset
  D_Flip_Flop d_ff_2 (
    .D(d_ff_2_qn), .clk(d_ff_1_qn), .Q(Output_bus_1[1]), .Qn(d_ff_2_qn), .reset(or_1_out));  // open: preset
  or or_1 (or_1_out, Input_2, Input_3);
  D_Flip_Flop d_ff_3 (
    .D(d_ff_3_qn), .clk(d_ff_2_qn), .Q(Output_bus_1[2]), .Qn(d_ff_3_qn), .reset(or_1_out));  // open: preset
  D_Flip_Flop d_ff_4 (
    .D(d_ff_4_qn), .clk(d_ff_3_qn), .Q(Output_bus_1[3]), .Qn(d_ff_4_qn), .reset(or_1_out));  // open: preset
endmodule
