// Logisim project Selector.circ as structural Verilog: 1 circuit, main circuit main
module main (
  input  Input_1,
  input  Input_2,
  input  Input_3,
  output Output_1,
  output Output_2,
  output Output_3,
  output Output_4,
  output Output_5,
  output Output_6
);

  wire a, and_2_out, and_3_out, and_4_out, and_5_out, and_6_out, and_7_out, and_8_out, d_ff_1_qn, m1, m2, m3,
       m11, m22, m33, not_1_out, not_2_out, not_3_out, not_4_out, not_5_out, not_6_out, not_7_out, not_8_out,
       not_9_out, or_4_out, or_5_out, or_6_out, or_7_out, or_8_out;

  D_Flip_Flop d_ff_1 (.D(d_ff_1_qn), .clk(Input_2), .Q(Output_6), .Qn(d_ff_1_qn), .reset(Input_3));  // open: preset
  and and_1 (a, Input_1, Output_6);
  not not_1 (not_1_out, m1);
  not not_2 (not_2_out, m2);
  not not_3 (not_3_out, m3);
  not not_4 (not_4_out, 1'b1);
  D_Flip_Flop d_ff_2 (.D(m11), .clk(a), .Q(m1), .reset(Input_3));  // open: Qn, preset
  D_Flip_Flop d_ff_3 (.D(m22), .clk(a), .Q(m2), .preset(Input_3));  // open: Qn, reset
  D_Flip_Flop d_ff_4 (.D(m33), .clk(a), .Q(m3), .preset(Input_3));  // open: Qn, reset
  and and_2 (and_2_out, not_1_out, m2, m3, 1'b1);
  or or_1 (m11, and_2_out, and_3_out);
  and and_3 (and_3_out, m1, not_2_out, not_3_out, not_4_out);
  and and_4 (and_4_out, not_1_out, not_2_out, m3, 1'b1);
  and and_5 (and_5_out, not_1_out, m2, not_3_out);
  or or_2 (m22, and_4_out, and_5_out, and_6_out);
  and and_6 (and_6_out, not_1_out, m2, not_4_out);
  and and_7 (and_7_out, not_1_out, not_3_out, 1'b1);
  or or_3 (m33, and_7_out, and_8_out);
  and and_8 (and_8_out, not_1_out, m3, not_4_out);
  not not_5 (not_5_out, m33);
  not not_6 (not_6_out, m22);
  not not_7 (not_7_out, m33);
  not not_8 (not_8_out, m22);
  not not_9 (not_9_out, m11);
  or or_4 (or_4_out, m33, m22, m11, 1'b0);
  or or_5 (or_5_out, not_5_out, m22, m11, 1'b0);
  or or_6 (or_6_out, m33, not_6_out, m11, 1'b0);
  or or_7 (or_7_out, not_7_out, not_8_out, m11, 1'b0);
  or or_8 (or_8_out, m33, m22, not_9_out, 1'b0);
  not not_10 (Output_1, or_4_out);
  not not_11 (Output_2, or_5_out);
  not not_12 (Output_3, or_6_out);
  not not_13 (Output_4, or_7_out);
  not not_14 (Output_5, or_8_out);
endmodule
