// Logisim project harry.circ as structural Verilog: 1 circuit, main circuit main
module main (
  input  ONOFF,
  input  RESET,
  output V
);

  wire and_1_out, BPM_out, clock_1_out, clock_2_out, clock_3_out, clock_4_out, clock_5_out, clock_6_out,
       clock_7_out, clock_8_out, clock_9_out, clock_10_out, clock_11_out, clock_12_out, clock_13_out,
       clock_14_out, d_ff_1_q, d_ff_2_q, d_ff_3_q, d_ff_4_q, d_ff_5_q, d_ff_6_q, d_ff_7_q, d_ff_8_q,
       d_ff_9_q, d_ff_10_q, d_ff_11_q, d_ff_12_q, d_ff_13_q, d_ff_14_q, d_ff_15_q, d_ff_16_q, d_ff_17_q,
       d_ff_18_q, d_ff_19_q, d_ff_20_q, d_ff_21_q, d_ff_22_q, d_ff_23_q, d_ff_24_q, d_ff_25_q, d_ff_26_q,
       d_ff_27_q, d_ff_28_q, d_ff_29_q, d_ff_30_q, d_ff_31_q, d_ff_32_q, d_ff_33_q, d_ff_34_q, d_ff_35_q,
       d_ff_36_q, d_ff_37_q, d_ff_38_q, d_ff_39_q, d_ff_40_q, d_ff_41_q, d_ff_42_q, d_ff_43_q, d_ff_44_q,
       d_ff_45_q, d_ff_46_q, d_ff_47_q, d_ff_48_q, d_ff_49_q, d_ff_50_q, d_ff_51_q, d_ff_52_q, d_ff_53_q,
       d_ff_54_q, d_ff_55_q, d_ff_56_q, d_ff_57_q, d_ff_58_q, d_ff_59_q, d_ff_60_q, d_ff_61_q, d_ff_62_q,
       d_ff_63_q, d_ff_64_q, multiplexer_1_out, multiplexer_2_out, multiplexer_3_out, multiplexer_4_out,
       multiplexer_5_out, multiplexer_6_out, multiplexer_7_out, multiplexer_8_out, multiplexer_9_out,
       multiplexer_10_out, multiplexer_11_out, multiplexer_12_out, multiplexer_13_out, multiplexer_14_out,
       multiplexer_15_out, or_1_out, or_2_out, or_3_out, or_4_out, or_5_out, or_6_out;

  Clock #(.highDuration(1600), .lowDuration(1600)) BPM (.out(BPM_out));
  Multiplexer multiplexer_1 (.in0(1'b0), .in1(BPM_out), .out(multiplexer_1_out), .sel(and_1_out));
  and and_1 (and_1_out, ONOFF, 1'b1);
  D_Flip_Flop d_ff_1 (.D(d_ff_64_q), .clk(multiplexer_1_out), .Q(d_ff_1_q), .reset(RESET));  // open: Qn, preset
  D_Flip_Flop d_ff_2 (.D(d_ff_49_q), .clk(multiplexer_1_out), .Q(d_ff_2_q), .reset(RESET));  // open: Qn, preset
  D_Flip_Flop d_ff_3 (.D(d_ff_50_q), .clk(multiplexer_1_out), .Q(d_ff_3_q), .reset(RESET));  // open: Qn, preset
  D_Flip_Flop d_ff_4 (.D(d_ff_51_q), .clk(multiplexer_1_out), .Q(d_ff_4_q), .reset(RESET));  // open: Qn, preset
  D_Flip_Flop d_ff_5 (.D(d_ff_52_q), .clk(multiplexer_1_out), .Q(d_ff_5_q), .reset(RESET));  // open: Qn, preset
  D_Flip_Flop d_ff_6 (.D(d_ff_53_q), .clk(multiplexer_1_out), .Q(d_ff_6_q), .reset(RESET));  // open: Qn, preset
  D_Flip_Flop d_ff_7 (.D(d_ff_54_q), .clk(multiplexer_1_out), .Q(d_ff_7_q), .reset(RESET));  // open: Qn, preset
  D_Flip_Flop d_ff_8 (.D(d_ff_55_q), .clk(multiplexer_1_out), .Q(d_ff_8_q), .reset(RESET));  // open: Qn, preset
  D_Flip_Flop d_ff_9 (.D(d_ff_56_q), .clk(multiplexer_1_out), .Q(d_ff_9_q), .reset(RESET));  // open: Qn, preset
  D_Flip_Flop d_ff_10 (.D(d_ff_57_q), .clk(multiplexer_1_out), .Q(d_ff_10_q), .reset(RESET));  // open: Qn, preset
  D_Flip_Flop d_ff_11 (.D(d_ff_58_q), .clk(multiplexer_1_out), .Q(d_ff_11_q), .reset(RESET));  // open: Qn, preset
  D_Flip_Flop d_ff_12 (.D(d_ff_59_q), .clk(multiplexer_1_out), .Q(d_ff_12_q), .reset(RESET));  // open: Qn, preset
  D_Flip_Flop d_ff_13 (.D(d_ff_60_q), .clk(multiplexer_1_out), .Q(d_ff_13_q), .reset(RESET));  // open: Qn, preset
  D_Flip_Flop d_ff_14 (.D(d_ff_61_q), .clk(multiplexer_1_out), .Q(d_ff_14_q), .reset(RESET));  // open: Qn, preset
  D_Flip_Flop d_ff_15 (.D(d_ff_62_q), .clk(multiplexer_1_out), .Q(d_ff_15_q), .reset(RESET));  // open: Qn, preset
  D_Flip_Flop d_ff_16 (.D(d_ff_63_q), .clk(multiplexer_1_out), .Q(d_ff_16_q), .reset(RESET));  // open: Qn, preset
  D_Flip_Flop d_ff_17 (.D(d_ff_1_q), .clk(multiplexer_1_out), .Q(d_ff_17_q), .reset(RESET));  // open: Qn, preset
  D_Flip_Flop d_ff_18 (.D(d_ff_2_q), .clk(multiplexer_1_out), .Q(d_ff_18_q), .reset(RESET));  // open: Qn, preset
  D_Flip_Flop d_ff_19 (.D(d_ff_3_q), .clk(multiplexer_1_out), .Q(d_ff_19_q), .reset(RESET));  // open: Qn, preset
  D_Flip_Flop d_ff_20 (.D(d_ff_4_q), .clk(multiplexer_1_out), .Q(d_ff_20_q), .reset(RESET));  // open: Qn, preset
  D_Flip_Flop d_ff_21 (.D(d_ff_5_q), .clk(multiplexer_1_out), .Q(d_ff_21_q), .reset(RESET));  // open: Qn, preset
  D_Flip_Flop d_ff_22 (.D(d_ff_6_q), .clk(multiplexer_1_out), .Q(d_ff_22_q), .reset(RESET));  // open: Qn, preset
  D_Flip_Flop d_ff_23 (.D(d_ff_7_q), .clk(multiplexer_1_out), .Q(d_ff_23_q), .reset(RESET));  // open: Qn, preset
  D_Flip_Flop d_ff_24 (.D(d_ff_8_q), .clk(multiplexer_1_out), .Q(d_ff_24_q), .reset(RESET));  // open: Qn, preset
  D_Flip_Flop d_ff_25 (.D(d_ff_9_q), .clk(multiplexer_1_out), .Q(d_ff_25_q), .reset(RESET));  // open: Qn, preset
  D_Flip_Flop d_ff_26 (.D(d_ff_10_q), .clk(multiplexer_1_out), .Q(d_ff_26_q), .reset(RESET));  // open: Qn, preset
  D_Flip_Flop d_ff_27 (.D(d_ff_11_q), .clk(multiplexer_1_out), .Q(d_ff_27_q), .reset(RESET));  // open: Qn, preset
  D_Flip_Flop d_ff_28 (.D(d_ff_12_q), .clk(multiplexer_1_out), .Q(d_ff_28_q), .reset(RESET));  // open: Qn, preset
  D_Flip_Flop d_ff_29 (.D(d_ff_13_q), .clk(multiplexer_1_out), .Q(d_ff_29_q), .reset(RESET));  // open: Qn, preset
  D_Flip_Flop d_ff_30 (.D(d_ff_14_q), .clk(multiplexer_1_out), .Q(d_ff_30_q), .reset(RESET));  // open: Qn, preset
  D_Flip_Flop d_ff_31 (.D(d_ff_15_q), .clk(multiplexer_1_out), .Q(d_ff_31_q), .reset(RESET));  // open: Qn, preset
  D_Flip_Flop d_ff_32 (.D(d_ff_16_q), .clk(multiplexer_1_out), .Q(d_ff_32_q), .reset(RESET));  // open: Qn, preset
  D_Flip_Flop d_ff_33 (.D(d_ff_17_q), .clk(multiplexer_1_out), .Q(d_ff_33_q), .reset(RESET));  // open: Qn, preset
  D_Flip_Flop d_ff_34 (.D(d_ff_18_q), .clk(multiplexer_1_out), .Q(d_ff_34_q), .reset(RESET));  // open: Qn, preset
  D_Flip_Flop d_ff_35 (.D(d_ff_19_q), .clk(multiplexer_1_out), .Q(d_ff_35_q), .reset(RESET));  // open: Qn, preset
  D_Flip_Flop d_ff_36 (.D(d_ff_20_q), .clk(multiplexer_1_out), .Q(d_ff_36_q), .reset(RESET));  // open: Qn, preset
  D_Flip_Flop d_ff_37 (.D(d_ff_21_q), .clk(multiplexer_1_out), .Q(d_ff_37_q), .reset(RESET));  // open: Qn, preset
  D_Flip_Flop d_ff_38 (.D(d_ff_22_q), .clk(multiplexer_1_out), .Q(d_ff_38_q), .reset(RESET));  // open: Qn, preset
  D_Flip_Flop d_ff_39 (.D(d_ff_23_q), .clk(multiplexer_1_out), .Q(d_ff_39_q), .reset(RESET));  // open: Qn, preset
  D_Flip_Flop d_ff_40 (.D(d_ff_24_q), .clk(multiplexer_1_out), .Q(d_ff_40_q), .reset(RESET));  // open: Qn, preset
  D_Flip_Flop d_ff_41 (.D(d_ff_25_q), .clk(multiplexer_1_out), .Q(d_ff_41_q), .reset(RESET));  // open: Qn, preset
  D_Flip_Flop d_ff_42 (.D(d_ff_26_q), .clk(multiplexer_1_out), .Q(d_ff_42_q), .reset(RESET));  // open: Qn, preset
  D_Flip_Flop d_ff_43 (.D(d_ff_27_q), .clk(multiplexer_1_out), .Q(d_ff_43_q), .reset(RESET));  // open: Qn, preset
  D_Flip_Flop d_ff_44 (.D(d_ff_28_q), .clk(multiplexer_1_out), .Q(d_ff_44_q), .reset(RESET));  // open: Qn, preset
  D_Flip_Flop d_ff_45 (.D(d_ff_29_q), .clk(multiplexer_1_out), .Q(d_ff_45_q), .reset(RESET));  // open: Qn, preset
  D_Flip_Flop d_ff_46 (.D(d_ff_30_q), .clk(multiplexer_1_out), .Q(d_ff_46_q), .reset(RESET));  // open: Qn, preset
  D_Flip_Flop d_ff_47 (.D(d_ff_31_q), .clk(multiplexer_1_out), .Q(d_ff_47_q), .reset(RESET));  // open: Qn, preset
  D_Flip_Flop d_ff_48 (.D(d_ff_32_q), .clk(multiplexer_1_out), .Q(d_ff_48_q), .reset(RESET));  // open: Qn, preset
  D_Flip_Flop d_ff_49 (.D(d_ff_33_q), .clk(multiplexer_1_out), .Q(d_ff_49_q), .reset(RESET));  // open: Qn, preset
  D_Flip_Flop d_ff_50 (.D(d_ff_34_q), .clk(multiplexer_1_out), .Q(d_ff_50_q), .reset(RESET));  // open: Qn, preset
  D_Flip_Flop d_ff_51 (.D(d_ff_35_q), .clk(multiplexer_1_out), .Q(d_ff_51_q), .reset(RESET));  // open: Qn, preset
  D_Flip_Flop d_ff_52 (.D(d_ff_36_q), .clk(multiplexer_1_out), .Q(d_ff_52_q), .reset(RESET));  // open: Qn, preset
  D_Flip_Flop d_ff_53 (.D(d_ff_37_q), .clk(multiplexer_1_out), .Q(d_ff_53_q), .reset(RESET));  // open: Qn, preset
  D_Flip_Flop d_ff_54 (.D(d_ff_38_q), .clk(multiplexer_1_out), .Q(d_ff_54_q), .reset(RESET));  // open: Qn, preset
  D_Flip_Flop d_ff_55 (.D(d_ff_39_q), .clk(multiplexer_1_out), .Q(d_ff_55_q), .reset(RESET));  // open: Qn, preset
  D_Flip_Flop d_ff_56 (.D(d_ff_40_q), .clk(multiplexer_1_out), .Q(d_ff_56_q), .reset(RESET));  // open: Qn, preset
  D_Flip_Flop d_ff_57 (.D(d_ff_41_q), .clk(multiplexer_1_out), .Q(d_ff_57_q), .reset(RESET));  // open: Qn, preset
  D_Flip_Flop d_ff_58 (.D(d_ff_42_q), .clk(multiplexer_1_out), .Q(d_ff_58_q), .reset(RESET));  // open: Qn, preset
  D_Flip_Flop d_ff_59 (.D(d_ff_43_q), .clk(multiplexer_1_out), .Q(d_ff_59_q), .reset(RESET));  // open: Qn, preset
  D_Flip_Flop d_ff_60 (.D(d_ff_44_q), .clk(multiplexer_1_out), .Q(d_ff_60_q), .reset(RESET));  // open: Qn, preset
  D_Flip_Flop d_ff_61 (.D(d_ff_45_q), .clk(multiplexer_1_out), .Q(d_ff_61_q), .reset(RESET));  // open: Qn, preset
  D_Flip_Flop d_ff_62 (.D(d_ff_46_q), .clk(multiplexer_1_out), .Q(d_ff_62_q), .reset(RESET));  // open: Qn, preset
  D_Flip_Flop d_ff_63 (.D(d_ff_47_q), .clk(multiplexer_1_out), .Q(d_ff_63_q), .reset(RESET));  // open: Qn, preset
  D_Flip_Flop d_ff_64 (.D(d_ff_48_q), .clk(multiplexer_1_out), .Q(d_ff_64_q), .preset(RESET));  // open: Qn, reset
  or or_1 (or_1_out, d_ff_18_q, d_ff_23_q, d_ff_12_q, d_ff_30_q);
  Multiplexer multiplexer_2 (.in0(1'b0), .in1(clock_1_out), .out(multiplexer_2_out), .sel(or_1_out));
  Clock #(.highDuration(3914), .lowDuration(3914)) clock_1 (.out(clock_1_out));
  or or_2 (or_2_out, d_ff_33_q, d_ff_3_q, d_ff_38_q, d_ff_27_q, d_ff_60_q);
  or or_3 (or_3_out, d_ff_1_q, d_ff_41_q, d_ff_58_q);
  or or_4 (or_4_out, d_ff_4_q, d_ff_61_q);
  Multiplexer multiplexer_3 (.in0(1'b0), .in1(clock_2_out), .out(multiplexer_3_out), .sel(or_2_out));
  Clock #(.highDuration(4655), .lowDuration(4655)) clock_2 (.out(clock_2_out));
  Multiplexer multiplexer_4 (.in0(1'b0), .in1(clock_3_out), .out(multiplexer_4_out), .sel(d_ff_63_q));
  Clock #(.highDuration(2932), .lowDuration(2932)) clock_3 (.out(clock_3_out));
  Multiplexer multiplexer_5 (.in0(1'b0), .in1(clock_4_out), .out(multiplexer_5_out), .sel(or_3_out));
  Clock #(.highDuration(6213), .lowDuration(6213)) clock_4 (.out(clock_4_out));
  Multiplexer multiplexer_6 (.in0(1'b0), .in1(clock_5_out), .out(multiplexer_6_out), .sel(or_4_out));
  Clock #(.highDuration(3107), .lowDuration(3107)) clock_5 (.out(clock_5_out));
  Multiplexer multiplexer_7 (.in0(1'b0), .in1(clock_6_out), .out(multiplexer_7_out), .sel(d_ff_30_q));
  Clock #(.highDuration(3291), .lowDuration(3291)) clock_6 (.out(clock_6_out));
  Clock #(.highDuration(5224), .lowDuration(5224)) clock_7 (.out(clock_7_out));
  Clock #(.highDuration(2612), .lowDuration(2612)) clock_8 (.out(clock_8_out));
  Multiplexer multiplexer_8 (.in0(1'b0), .in1(clock_7_out), .out(multiplexer_8_out), .sel(d_ff_30_q));
  Multiplexer multiplexer_9 (.in0(1'b0), .in1(clock_8_out), .out(multiplexer_9_out), .sel(d_ff_8_q));
  Multiplexer multiplexer_10 (.in0(1'b0), .in1(clock_9_out), .out(multiplexer_10_out), .sel(d_ff_31_q));
  Clock #(.highDuration(2768), .lowDuration(2768)) clock_9 (.out(clock_9_out));
  Multiplexer multiplexer_11 (.in0(1'b0), .in1(clock_10_out), .out(multiplexer_11_out), .sel(d_ff_36_q));
  Clock #(.highDuration(3487), .lowDuration(3487)) clock_10 (.out(clock_10_out));
  Clock #(.highDuration(6582), .lowDuration(6582)) clock_11 (.out(clock_11_out));
  Multiplexer multiplexer_12 (.in0(1'b0), .in1(clock_11_out), .out(multiplexer_12_out), .sel(d_ff_8_q));
  Multiplexer multiplexer_13 (.in0(1'b0), .in1(clock_12_out), .out(multiplexer_13_out), .sel(d_ff_63_q));
  Clock #(.highDuration(3694), .lowDuration(3694)) clock_12 (.out(clock_12_out));
  or or_5 (or_5_out, d_ff_34_q, d_ff_39_q, d_ff_37_q, d_ff_28_q);
  or or_6 (or_6_out, d_ff_9_q, d_ff_63_q);
  Multiplexer multiplexer_14 (.in0(1'b0), .in1(clock_13_out), .out(multiplexer_14_out), .sel(or_5_out));
  Clock #(.highDuration(4147), .lowDuration(4147)) clock_13 (.out(clock_13_out));
  Multiplexer multiplexer_15 (.in0(1'b0), .in1(clock_14_out), .out(multiplexer_15_out), .sel(or_6_out));
  Clock #(.highDuration(4393), .lowDuration(4393)) clock_14 (.out(clock_14_out));
  or or_7 (V, multiplexer_2_out, multiplexer_3_out, multiplexer_4_out, multiplexer_5_out, multiplexer_6_out, multiplexer_7_out, multiplexer_8_out, multiplexer_9_out, multiplexer_10_out, multiplexer_11_out, multiplexer_12_out, multiplexer_13_out, multiplexer_14_out, multiplexer_15_out);

  // Notes on the sheet:
  //   DO
  //   LA
  //   FA
  //   MI min
  //   MI maj
  //   MI b
  //   SOL min
  //   SOL maj
  //   SOL b
  //   RE
  //   RE#
  //   RE b
  //   SI
  //   SI b
endmodule
