// Logisim project main_project.circ as structural Verilog: 51 circuits, main circuit Switch_1
module main (
  input  Input_1,
  input  Input_2,
  input  Input_3,
  input  Input_4,
  input  Input_5,
  output Output_1,
  output Output_2,
  output Output_3,
  output Output_4,
  output Output_5,
  output Output_6,
  output Output_7,
  output Output_8,
  output Output_9,
  output Output_10,
  output Output_11,
  output Output_12,
  output Output_13
);

  wire A, A_1, and_1_out, and_3_out, B, B_1, B_star, B_star_1, Chrono_On, clock_1_out, Desc_2_1_output_1,
       Descendant_1_output_1, Descendant_2_output_1, Descendant_3_output_1, DIP_1, Dip_2, DIP_3, DIP_4,
       DIP_5, DIP_THREE, DIR, DISPLAY_C, E, Enter, Filtre_4_output_1, Filtre_6_output_1, Filtre_7_output_1,
       Harry_Song_1_v, Horloge_On, Lettre_a_Elise_1_v, Long_press_1_output_1, Minuteur_On,
       Montant_3_output_1, multiplexer_4_out, multiplexer_5_out, multiplexer_8_out, multiplexer_9_out,
       or_2_out, or_3_out, or_4_out, or_5_out, or_6_out, or_9_out, or_11_out, or_12_out, Reset_Chrono,
       Reset_G, Reset_Min, Reset_Setting, Set_Hour, Setting_On, Setting_On_1, Setting_On_2, Sonnerie_Alarm,
       Sonnerie_Minuteur, Start_Alarm, Start_Chrono, Start_Minuteur;
  wire [3:0] Chrono_2_1_output_bus_1, Chrono_2_1_output_bus_2, Chrono_2_1_output_bus_3,
       Chrono_2_1_output_bus_4, Chrono_2_1_output_bus_5, Chrono_2_1_output_bus_6,
       Display_Off_2_1_output_bus_1, Display_Off_2_1_output_bus_2, Display_Off_2_1_output_bus_3,
       Display_Off_2_1_output_bus_4, Display_Off_2_1_output_bus_5, Display_Off_2_1_output_bus_6;
  wire [23:0] Minuteur_1_output_bus_1, Sortie_Setting, Sortie_Setting_1, Sortie_Setting_2, Sortie_Watch;
  wire [47:0] affichage_inverse_1_1_output_bus_1, Convert_All_1_output_bus_1, Convert_All_2_output_bus_1,
       DISPLAY, multiplexer_10_out, multiplexer_11_out;

  // DipSwitch #(.number(5)) DipSwitch_1: pin names not known; wires that end beside it: DIP_1, Dip_2, DIP_3, DIP_4, DIP_5
  or or_1 (DIP_THREE, DIP_1, Dip_2, DIP_3);
  Multiplexer multiplexer_1 (.in0(1'b0), .in1(Input_1), .out(E), .sel(DIP_4));
  Multiplexer multiplexer_2 (.in0(1'b0), .in1(Input_2), .out(A_1), .sel(DIP_4));
  Multiplexer multiplexer_3 (.in0(1'b0), .in1(Input_3), .out(B_1), .sel(DIP_4));
  Multiplexer multiplexer_4 (.in0(1'b0), .in1(Input_4), .out(multiplexer_4_out), .sel(DIP_4));
  Multiplexer multiplexer_5 (.in0(1'b0), .in1(Input_5), .out(multiplexer_5_out), .sel(DIP_4));
  or or_2 (or_2_out, Output_5, Output_6);
  and and_1 (and_1_out, A_1, B_1);
  or or_3 (or_3_out, Reset_G, ~Sonnerie_Alarm, Start_Alarm);  // OR_Gate
  or or_4 (or_4_out, Reset_G, ~Sonnerie_Minuteur, Start_Minuteur);  // OR_Gate
  and and_2 (Setting_On_1, or_2_out, Output_8);
  or or_5 (or_5_out, Reset_Setting, Reset_G);
  and and_3 (and_3_out, B, Sonnerie_Alarm);
  Multiplexer #(.width(24)) multiplexer_6 (
    .in0(Sortie_Setting_1), .in1(Sortie_Setting_2), .out(Sortie_Setting), .sel(Setting_On_2));
  and and_4 (Setting_On_2, Output_3, Output_8);
  or or_6 (or_6_out, and_3_out, Reset_G);
  Long_press Long_press_1 (.Input_1(and_1_out), .Output_1(Long_press_1_output_1));
  Montant Montant_1 (.Input_1(Output_8), .Output_1(Reset_Chrono));  // open: Input_2
  Montant Montant_2 (.Input_1(Output_8), .Output_1(Reset_Setting));  // open: Input_2
  Trans_HELLO aaaa_1 (.Input_1(DIP_4), .Input_2(Reset_G), .Output_bus_1(DISPLAY), .Output_1(DISPLAY_C));
  Filtre Filtre_1 (.Input_1(E), .Output_1(Enter));
  Filtre Filtre_2 (.Input_1(A_1), .Output_1(A));
  Filtre Filtre_3 (.Input_1(B_1), .Output_1(B));
  Filtre Filtre_6 (.Input_1(multiplexer_4_out), .Output_1(Filtre_6_output_1));
  Filtre Filtre_7 (.Input_1(multiplexer_5_out), .Output_1(Filtre_7_output_1));
  Multiplexer multiplexer_7 (.in0(B_star), .in1(1'b0), .out(B_star_1), .sel(DIP_THREE));
  Harry_Song Harry_Song_1 (.ONOFF(Sonnerie_Alarm), .RESET(or_3_out), .V(Harry_Song_1_v));
  Lettre_a_Elise Lettre_a_Elise_1 (.ONOFF(Sonnerie_Minuteur), .RESET(or_4_out), .V(Lettre_a_Elise_1_v));
  or or_7 (Reset_G, Long_press_1_output_1, ~DIP_4);  // OR_Gate
  or or_8 (Output_9, Harry_Song_1_v, Lettre_a_Elise_1_v);
  Setting Setting_1 (
    .ENTER(Setting_On_1), .A(A), .B(B), .DIP_1(DIP_1), .DIP_2(Dip_2), .DIP_3(DIP_3), .RST(or_5_out),
    .Output_bus_1(Sortie_Setting_1[3:0]), .Output_bus_2(Sortie_Setting_1[7:4]),
    .Output_bus_3(Sortie_Setting_1[11:8]), .Output_bus_4(Sortie_Setting_1[15:12]),
    .Output_bus_5(Sortie_Setting_1[19:16]), .Output_bus_6(Sortie_Setting_1[23:20]));
  Setting Setting_2 (
    .ENTER(Setting_On_2), .A(A), .B(B), .DIP_1(DIP_1), .DIP_2(Dip_2), .DIP_3(DIP_3), .RST(or_6_out),
    .Output_bus_1(Sortie_Setting_2[3:0]), .Output_bus_2(Sortie_Setting_2[7:4]),
    .Output_bus_3(Sortie_Setting_2[11:8]), .Output_bus_4(Sortie_Setting_2[15:12]),
    .Output_bus_5(Sortie_Setting_2[19:16]), .Output_bus_6(Sortie_Setting_2[23:20]));
  Encodeur Encodeur_1 (.CHA(Filtre_6_output_1), .CHB(Filtre_7_output_1), .UpDown(DIR), .G5(B_star));
  or or_9 (or_9_out, Chrono_On, Minuteur_On, Output_8);
  or or_10 (Setting_On, Setting_On_1, Setting_On_2);
  not not_1 (Horloge_On, or_9_out);
  Selector Selector_1 (
    .Input_1(Enter), .Input_2(B_star_1), .Input_4(DIR), .Input_3(Reset_G), .Output_1(Output_3),
    .Output_2(Output_4), .Output_3(Output_5), .Output_4(Output_6), .Output_5(Output_7), .Output_6(Output_8));
  Clock #(.highDuration(17000), .lowDuration(17000)) clock_1 (.out(clock_1_out));
  Filtre Filtre_4 (.Input_1(Output_8), .Output_1(Filtre_4_output_1));
  Descendant Descendant_1 (.Input_1(Output_8), .Output_1(Descendant_1_output_1));  // open: Input_2
  Descendant Descendant_2 (.Input_1(Output_8), .Output_1(Descendant_2_output_1));  // open: Input_2
  Descendant Descendant_3 (.Input_1(Output_8), .Output_1(Descendant_3_output_1));  // open: Input_2
  Montant Montant_3 (.Input_1(Output_8), .Output_1(Montant_3_output_1));  // open: Input_2
  Multiplexer multiplexer_8 (.in0(1'b0), .in1(B), .out(multiplexer_8_out), .sel(Sonnerie_Alarm));
  or or_11 (or_11_out, Reset_G, Reset_Min);
  Multiplexer multiplexer_9 (.in0(1'b0), .in1(clock_1_out), .out(multiplexer_9_out), .sel(DIP_4));
  and and_5 (Set_Hour, Descendant_1_output_1, Output_6);
  and and_6 (Start_Alarm, Descendant_2_output_1, Output_3);
  and and_7 (Start_Minuteur, Descendant_3_output_1, Output_5);
  and and_8 (Reset_Min, Montant_3_output_1, Output_5);
  or or_12 (or_12_out, Reset_G, Reset_Chrono);
  Desc_2 Desc_2_1 (.Input_1(Filtre_4_output_1), .Input_2(Reset_G), .Output_1(Desc_2_1_output_1));
  and and_9 (Start_Chrono, Desc_2_1_output_1, Output_4);
  Alarm Alarm_1 (
    .Heure_Courante(Sortie_Watch), .Heure_Reveil(Sortie_Setting_2), .long_press(Start_Alarm),
    .Stop(multiplexer_8_out), .Reset_alarm(Reset_G), .S(Sonnerie_Alarm));
  Chrono Chrono_2_1 (
    .ENTER(Start_Chrono), .A(A), .B(B), .RST_G(or_12_out), .Output_bus_1(Chrono_2_1_output_bus_1),
    .Output_bus_2(Chrono_2_1_output_bus_2), .Output_bus_3(Chrono_2_1_output_bus_3),
    .Output_bus_4(Chrono_2_1_output_bus_4), .Output_bus_5(Chrono_2_1_output_bus_5),
    .Output_bus_6(Chrono_2_1_output_bus_6), .On_Off(Chrono_On));
  Minuteur Minuteur_1 (
    .ENTER(Start_Minuteur), .A(A), .STOP(B), .RST(or_11_out), .Binary_Entrance(Sortie_Setting_1),
    .Input_1(clock_1_out), .Output_bus_1(Minuteur_1_output_bus_1), .On_Off(Minuteur_On),
    .Sonnerie_Min(Sonnerie_Minuteur));
  Watch_test Watch_test_1 (
    .CLOCK(multiplexer_9_out), .RST(Reset_G), .Long_Press(Set_Hour), .Binary_Entrance(Sortie_Setting_1),
    .Output_bus_1(Sortie_Watch[3:0]), .Output_bus_2(Sortie_Watch[7:4]), .Output_bus_3(Sortie_Watch[11:8]),
    .Output_bus_4(Sortie_Watch[15:12]), .Output_bus_5(Sortie_Watch[19:16]), .Output_bus_6(Sortie_Watch[23:20]));
  Display_Off_2 Display_Off_2_1 (
    .Input_bus_7(Chrono_2_1_output_bus_1), .Input_bus_8(Chrono_2_1_output_bus_2),
    .Input_bus_9(Chrono_2_1_output_bus_3), .Input_bus_10(Chrono_2_1_output_bus_4),
    .Input_bus_11(Chrono_2_1_output_bus_5), .Input_bus_12(Chrono_2_1_output_bus_6),
    .Input_bus_13(Minuteur_1_output_bus_1[23:20]), .Input_bus_14(Minuteur_1_output_bus_1[19:16]),
    .Input_bus_15(Minuteur_1_output_bus_1[15:12]), .Input_bus_16(Minuteur_1_output_bus_1[11:8]),
    .Input_bus_17(Minuteur_1_output_bus_1[7:4]), .Input_bus_18(Minuteur_1_output_bus_1[3:0]),
    .Input_bus_19(Sortie_Watch[3:0]), .Input_bus_20(Sortie_Watch[7:4]), .Input_bus_21(Sortie_Watch[11:8]),
    .Input_bus_22(Sortie_Watch[15:12]), .Input_bus_23(Sortie_Watch[19:16]),
    .Input_bus_24(Sortie_Watch[23:20]), .Input_bus_25(Sortie_Setting[3:0]),
    .Input_bus_26(Sortie_Setting[7:4]), .Input_bus_27(Sortie_Setting[11:8]),
    .Input_bus_28(Sortie_Setting[15:12]), .Input_bus_29(Sortie_Setting[19:16]),
    .Input_bus_30(Sortie_Setting[23:20]), .Input_1(Chrono_On), .Input_2(Minuteur_On), .Input_3(Horloge_On),
    .Input_4(Setting_On), .Output_bus_1(Display_Off_2_1_output_bus_1),
    .Output_bus_2(Display_Off_2_1_output_bus_2), .Output_bus_3(Display_Off_2_1_output_bus_3),
    .Output_bus_4(Display_Off_2_1_output_bus_4), .Output_bus_5(Display_Off_2_1_output_bus_5),
    .Output_bus_6(Display_Off_2_1_output_bus_6));  // open: Input_bus_1, Input_bus_2, Input_bus_3, Input_bus_4, Input_bus_5, Input_bus_6
  Convert_All Convert_All_2 (
    .Input_bus_1({Display_Off_2_1_output_bus_6, Display_Off_2_1_output_bus_5, Display_Off_2_1_output_bus_4, Display_Off_2_1_output_bus_3, Display_Off_2_1_output_bus_2, Display_Off_2_1_output_bus_1}),
    .Output_bus_1(Convert_All_2_output_bus_1));
  Convert_All Convert_All_1 (
    .Input_bus_1({Display_Off_2_1_output_bus_6, Display_Off_2_1_output_bus_5, Display_Off_2_1_output_bus_4, Display_Off_2_1_output_bus_3, Display_Off_2_1_output_bus_2, Display_Off_2_1_output_bus_1}),
    .Output_bus_1(Convert_All_1_output_bus_1));
  affichage_inverse_1 affichage_inverse_1_1 (
    .Input_bus_1(Convert_All_2_output_bus_1), .Output_bus_1(affichage_inverse_1_1_output_bus_1));
  Multiplexer #(.width(48)) multiplexer_10 (
    .in0(Convert_All_1_output_bus_1), .in1(affichage_inverse_1_1_output_bus_1), .out(multiplexer_10_out),
    .sel(DIP_5));
  Multiplexer #(.width(48)) multiplexer_11 (
    .in0(multiplexer_10_out), .in1(DISPLAY), .out(multiplexer_11_out), .sel(DISPLAY_C));
  _7_Segment_Display L_7_Segment_Display_1 (
    .g(multiplexer_11_out[6]), .f(multiplexer_11_out[5]), .a(multiplexer_11_out[0]),
    .b(multiplexer_11_out[1]), .e(multiplexer_11_out[4]), .d(multiplexer_11_out[3]),
    .c(multiplexer_11_out[2]), .dp(multiplexer_11_out[7]));
  _7_Segment_Display L_7_Segment_Display_2 (
    .g(multiplexer_11_out[14]), .f(multiplexer_11_out[13]), .a(multiplexer_11_out[8]),
    .b(multiplexer_11_out[9]), .e(multiplexer_11_out[12]), .d(multiplexer_11_out[11]),
    .c(multiplexer_11_out[10]), .dp(multiplexer_11_out[15]));
  _7_Segment_Display L_7_Segment_Display_3 (
    .g(multiplexer_11_out[22]), .f(multiplexer_11_out[21]), .a(multiplexer_11_out[16]),
    .b(multiplexer_11_out[17]), .e(multiplexer_11_out[20]), .d(multiplexer_11_out[19]),
    .c(multiplexer_11_out[18]), .dp(multiplexer_11_out[23]));
  _7_Segment_Display L_7_Segment_Display_4 (
    .g(multiplexer_11_out[30]), .f(multiplexer_11_out[29]), .a(multiplexer_11_out[24]),
    .b(multiplexer_11_out[25]), .e(multiplexer_11_out[28]), .d(multiplexer_11_out[27]),
    .c(multiplexer_11_out[26]), .dp(multiplexer_11_out[31]));
  _7_Segment_Display L_7_Segment_Display_5 (
    .g(multiplexer_11_out[38]), .f(multiplexer_11_out[37]), .a(multiplexer_11_out[32]),
    .b(multiplexer_11_out[33]), .e(multiplexer_11_out[36]), .d(multiplexer_11_out[35]),
    .c(multiplexer_11_out[34]), .dp(multiplexer_11_out[39]));
  _7_Segment_Display L_7_Segment_Display_6 (
    .g(multiplexer_11_out[46]), .f(multiplexer_11_out[45]), .a(multiplexer_11_out[40]),
    .b(multiplexer_11_out[41]), .e(multiplexer_11_out[44]), .d(multiplexer_11_out[43]),
    .c(multiplexer_11_out[42]), .dp(multiplexer_11_out[47]));

  assign Output_1 = 1'b1;
  assign Output_2 = 1'b0;
  assign Output_10 = 1'b0;
  assign Output_11 = 1'b0;
  assign Output_12 = 1'b0;
  assign Output_13 = 1'b0;

  // Other names for the same wires on the sheet: Alarme = Output_3; Chronos = Output_4; Horloge = Output_7;
  //   Minuteure = Output_5; Select_On = Output_8; Set_Clock = Output_6

  // Notes on the sheet:
  //   Fréquence de fonctionnement : 32kHz
endmodule

module Long_press (
  input  Input_1,
  output Output_1
);

  wire clock_1_out, d_ff_1_q, d_ff_2_q, d_ff_3_q;

  Clock #(.highDuration(17000), .lowDuration(17000)) clock_1 (.out(clock_1_out));
  D_Flip_Flop d_ff_1 (.D(Input_1), .clk(clock_1_out), .Q(d_ff_1_q));  // open: Qn, preset, reset
  D_Flip_Flop d_ff_2 (.D(d_ff_1_q), .clk(clock_1_out), .Q(d_ff_2_q));  // open: Qn, preset, reset
  D_Flip_Flop d_ff_3 (.D(d_ff_2_q), .clk(clock_1_out), .Q(d_ff_3_q));  // open: Qn, preset, reset
  and and_1 (Output_1, d_ff_1_q, d_ff_2_q, d_ff_3_q);
endmodule

module Switch_1 (
  input  Input_1,
  input  Input_2,
  output Output_1
);

  wire A, A1, and_1_out, and_2_out, clock_1_out, not_1_out, not_2_out, One_Tic_1_output_1;

  Clock #(.highDuration(10), .lowDuration(10)) clock_1 (.out(clock_1_out));
  D_Flip_Flop d_ff_1 (.D(A1), .clk(clock_1_out), .Q(A), .reset(Input_2));  // open: Qn, preset
  One_Tic One_Tic_1 (.Input_1(Input_1), .Input_2(clock_1_out), .Output_1(One_Tic_1_output_1));
  not not_1 (not_1_out, A);
  not not_2 (not_2_out, One_Tic_1_output_1);
  and and_1 (and_1_out, not_1_out, One_Tic_1_output_1);
  and and_2 (and_2_out, A, not_2_out);
  or or_1 (A1, and_1_out, and_2_out);
  Filtre Filtre_1 (.Input_1(A1), .Output_1(Output_1));
endmodule

module One_Tic (
  input  Input_1,
  input  Input_2,
  output Output_1
);

  wire d_ff_1_q, d_ff_1_qn, d_ff_2_q;

  D_Flip_Flop #(.trigger("falling")) d_ff_1 (
    .D(Input_1), .clk(Input_2), .Q(d_ff_1_q), .Qn(d_ff_1_qn));  // open: preset, reset
  D_Flip_Flop d_ff_2 (.D(d_ff_1_qn), .clk(Input_2), .Q(d_ff_2_q));  // open: Qn, preset, reset
  and and_1 (Output_1, d_ff_1_q, d_ff_2_q);
endmodule

module Debouncing (
  input  Input_1,
  input  Input_2,
  output Output_1
);

  wire and_1_out, and_2_out, d_ff_1_q, d_ff_2_q, d_ff_3_q, d_ff_4_q, nor_1_out;

  D_Flip_Flop d_ff_1 (.D(Input_1), .clk(Input_2), .Q(d_ff_1_q));  // open: Qn, preset, reset
  D_Flip_Flop d_ff_2 (.D(d_ff_1_q), .clk(Input_2), .Q(d_ff_2_q));  // open: Qn, preset, reset
  D_Flip_Flop d_ff_3 (.D(d_ff_2_q), .clk(Input_2), .Q(d_ff_3_q));  // open: Qn, preset, reset
  D_Flip_Flop d_ff_4 (.D(d_ff_3_q), .clk(Input_2), .Q(d_ff_4_q));  // open: Qn, preset, reset
  and and_1 (and_1_out, d_ff_1_q, d_ff_2_q, d_ff_3_q, d_ff_4_q);
  and and_2 (and_2_out, ~d_ff_4_q, ~d_ff_3_q, ~d_ff_2_q, ~d_ff_1_q);  // AND_Gate
  nor nor_1 (nor_1_out, and_1_out, Output_1);
  nor nor_2 (Output_1, nor_1_out, and_2_out);
endmodule

module Filtre (
  input  Input_1,
  output Output_1
);

  wire clock_1_out;

  Clock clock_1 (.out(clock_1_out));
  Debouncing Debouncing_1 (.Input_1(Input_1), .Input_2(clock_1_out), .Output_1(Output_1));
endmodule

module Montant (
  input  Input_1,
  input  Input_2,
  output Output_1
);

  wire clock_1_out, d_ff_1_qn;

  Clock clock_1 (.out(clock_1_out));
  D_Flip_Flop d_ff_1 (.D(Input_1), .clk(clock_1_out), .Qn(d_ff_1_qn), .reset(Input_2));  // open: Q, preset
  and and_1 (Output_1, Input_1, d_ff_1_qn);

  // Notes on the sheet:
  //   Flanc montant 
endmodule

module Descendant (
  input  Input_1,
  input  Input_2,
  output Output_1
);

  wire clock_1_out, d_ff_1_q, not_1_out;

  Clock clock_1 (.out(clock_1_out));
  D_Flip_Flop d_ff_1 (.D(Input_1), .clk(clock_1_out), .Q(d_ff_1_q), .reset(Input_2));  // open: Qn, preset
  not not_1 (not_1_out, Input_1);
  and and_1 (Output_1, not_1_out, d_ff_1_q);

  // Notes on the sheet:
  //   Flanc descendant 
endmodule

module Desc_2 (
  input  Input_1,
  input  Input_2,
  output Output_1
);

  wire clock_1_out, d_ff_1_q, not_1_out;

  Clock #(.highDuration(10), .lowDuration(10)) clock_1 (.out(clock_1_out));
  D_Flip_Flop d_ff_1 (.D(Input_1), .clk(clock_1_out), .Q(d_ff_1_q), .reset(Input_2));  // open: Qn, preset
  not not_1 (not_1_out, Input_1);
  and and_1 (Output_1, not_1_out, d_ff_1_q);

  // Notes on the sheet:
  //   Flanc descendant 
endmodule

module Transition_Selector (
  input  Input_1,
  input  Input_2,
  input  Input_3,
  input  Input_4,
  output Output_1,
  output Output_2,
  output Output_3
);

  wire and_1_out, and_2_out, and_3_out, and_4_out, and_5_out, and_6_out, and_7_out, not_1_out, not_2_out,
       not_3_out, not_4_out;

  not not_1 (not_1_out, Input_1);
  not not_2 (not_2_out, Input_2);
  not not_3 (not_3_out, Input_3);
  not not_4 (not_4_out, Input_4);
  and and_1 (and_1_out, not_1_out, Input_2);
  and and_2 (and_2_out, Input_1, Input_3, Input_4);
  and and_3 (and_3_out, not_1_out, Input_3);
  and and_4 (and_4_out, Input_3, not_4_out);
  and and_5 (and_5_out, Input_1, not_3_out, Input_4);
  and and_6 (and_6_out, not_1_out, Input_4);
  and and_7 (and_7_out, Input_1, not_2_out, not_4_out);
  or or_1 (Output_1, and_1_out, and_2_out);
  or or_2 (Output_2, and_3_out, and_4_out, and_5_out);
  or or_3 (Output_3, and_6_out, and_7_out);
endmodule

module Count_S (
  input  Input_1,
  input  Input_2,
  output [2:0] Output_bus_1
);

  wire B_STAR, clock_1_out, Transition_Selector_1_output_1, Transition_Selector_1_output_2,
       Transition_Selector_1_output_3;

  Montant Montant_1 (.Input_1(Input_1), .Input_2(Input_2), .Output_1(B_STAR));
  Transition_Selector Transition_Selector_1 (
    .Input_1(B_STAR), .Input_2(Output_bus_1[2]), .Input_3(Output_bus_1[1]), .Input_4(Output_bus_1[0]),
    .Output_1(Transition_Selector_1_output_1), .Output_2(Transition_Selector_1_output_2),
    .Output_3(Transition_Selector_1_output_3));
  D_Flip_Flop d_ff_1 (
    .D(Transition_Selector_1_output_1), .clk(clock_1_out), .Q(Output_bus_1[2]), .reset(Input_2));  // open: Qn, preset
  Clock clock_1 (.out(clock_1_out));
  D_Flip_Flop d_ff_2 (
    .D(Transition_Selector_1_output_2), .clk(clock_1_out), .Q(Output_bus_1[1]), .reset(Input_2));  // open: Qn, preset
  D_Flip_Flop d_ff_3 (
    .D(Transition_Selector_1_output_3), .clk(clock_1_out), .Q(Output_bus_1[0]), .reset(Input_2));  // open: Qn, preset

  // Other names for the same wires on the sheet: RST = Input_2
endmodule

module Selector (
  input  Input_1,
  input  Input_2,
  input  Input_4,
  input  Input_3,
  output Output_1,
  output Output_2,
  output Output_3,
  output Output_4,
  output Output_5,
  output Output_6
);

  wire and_1_out, and_2_out, multiplexer_1_out, multiplexer_2_out, or_1_out, or_2_out, or_3_out, or_4_out,
       or_5_out;
  wire [2:0] Test_1_output_bus_1;

  Switch_1 Switch_1_1 (.Input_1(Input_1), .Input_2(Input_3), .Output_1(Output_6));
  and and_1 (and_1_out, Input_2, Output_6);
  Multiplexer multiplexer_1 (.in0(and_1_out), .in1(1'b0), .out(multiplexer_1_out), .sel(Input_4));
  and and_2 (and_2_out, Input_2, Output_6);
  Multiplexer multiplexer_2 (.in0(1'b0), .in1(and_2_out), .out(multiplexer_2_out), .sel(Input_4));
  Count_Up_Down Test_1 (
    .LEFT(multiplexer_1_out), .RIGHT(multiplexer_2_out), .RST(Input_3), .Output_bus_1(Test_1_output_bus_1));
  or or_1 (or_1_out, Test_1_output_bus_1[0], Test_1_output_bus_1[1], Test_1_output_bus_1[2]);
  or or_2 (or_2_out, ~Test_1_output_bus_1[0], Test_1_output_bus_1[1], Test_1_output_bus_1[2]);  // OR_Gate
  not not_1 (Output_1, or_1_out);
  or or_3 (or_3_out, Test_1_output_bus_1[0], ~Test_1_output_bus_1[1], Test_1_output_bus_1[2]);  // OR_Gate
  not not_2 (Output_2, or_2_out);
  not not_3 (Output_3, or_3_out);
  not not_4 (Output_4, or_4_out);
  or or_4 (or_4_out, ~Test_1_output_bus_1[0], ~Test_1_output_bus_1[1], Test_1_output_bus_1[2]);  // OR_Gate
  not not_5 (Output_5, or_5_out);
  or or_5 (or_5_out, Test_1_output_bus_1[0], Test_1_output_bus_1[1], ~Test_1_output_bus_1[2]);  // OR_Gate

  // Other names for the same wires on the sheet: On_Off = Output_6
endmodule

module Display_Off_2 (
  input  [3:0] Input_bus_1,
  input  [3:0] Input_bus_2,
  input  [3:0] Input_bus_3,
  input  [3:0] Input_bus_4,
  input  [3:0] Input_bus_5,
  input  [3:0] Input_bus_6,
  input  [3:0] Input_bus_7,
  input  [3:0] Input_bus_8,
  input  [3:0] Input_bus_9,
  input  [3:0] Input_bus_10,
  input  [3:0] Input_bus_11,
  input  [3:0] Input_bus_12,
  input  [3:0] Input_bus_13,
  input  [3:0] Input_bus_14,
  input  [3:0] Input_bus_15,
  input  [3:0] Input_bus_16,
  input  [3:0] Input_bus_17,
  input  [3:0] Input_bus_18,
  input  [3:0] Input_bus_19,
  input  [3:0] Input_bus_20,
  input  [3:0] Input_bus_21,
  input  [3:0] Input_bus_22,
  input  [3:0] Input_bus_23,
  input  [3:0] Input_bus_24,
  input  [3:0] Input_bus_25,
  input  [3:0] Input_bus_26,
  input  [3:0] Input_bus_27,
  input  [3:0] Input_bus_28,
  input  [3:0] Input_bus_29,
  input  [3:0] Input_bus_30,
  input  Input_1,
  input  Input_2,
  input  Input_3,
  input  Input_4,
  output [3:0] Output_bus_1,
  output [3:0] Output_bus_2,
  output [3:0] Output_bus_3,
  output [3:0] Output_bus_4,
  output [3:0] Output_bus_5,
  output [3:0] Output_bus_6
);

  wire not_1_out;
  wire [3:0] multiplexer_1_out, multiplexer_2_out, multiplexer_3_out, multiplexer_4_out, multiplexer_5_out,
       multiplexer_6_out, multiplexer_7_out, multiplexer_8_out, multiplexer_9_out, multiplexer_10_out,
       multiplexer_11_out, multiplexer_12_out, multiplexer_13_out, multiplexer_14_out, multiplexer_15_out,
       multiplexer_16_out, multiplexer_17_out, multiplexer_18_out;

  not not_1 (not_1_out, Input_1);
  Multiplexer #(.width(4)) multiplexer_1 (
    .in0(Input_bus_7), .in1(Input_bus_1), .out(multiplexer_1_out), .sel(not_1_out));
  Multiplexer #(.width(4)) multiplexer_2 (
    .in0(Input_bus_8), .in1(Input_bus_2), .out(multiplexer_2_out), .sel(not_1_out));
  Multiplexer #(.width(4)) multiplexer_3 (
    .in0(Input_bus_9), .in1(Input_bus_3), .out(multiplexer_3_out), .sel(not_1_out));
  Multiplexer #(.width(4)) multiplexer_4 (
    .in0(Input_bus_10), .in1(Input_bus_4), .out(multiplexer_4_out), .sel(not_1_out));
  Multiplexer #(.width(4)) multiplexer_5 (
    .in0(Input_bus_11), .in1(Input_bus_5), .out(multiplexer_5_out), .sel(not_1_out));
  Multiplexer #(.width(4)) multiplexer_6 (
    .in0(Input_bus_12), .in1(Input_bus_6), .out(multiplexer_6_out), .sel(not_1_out));
  Multiplexer #(.width(4)) multiplexer_7 (
    .in0(multiplexer_1_out), .in1(Input_bus_13), .out(multiplexer_7_out), .sel(Input_2));
  Multiplexer #(.width(4)) multiplexer_8 (
    .in0(multiplexer_2_out), .in1(Input_bus_14), .out(multiplexer_8_out), .sel(Input_2));
  Multiplexer #(.width(4)) multiplexer_9 (
    .in0(multiplexer_3_out), .in1(Input_bus_15), .out(multiplexer_9_out), .sel(Input_2));
  Multiplexer #(.width(4)) multiplexer_10 (
    .in0(multiplexer_4_out), .in1(Input_bus_16), .out(multiplexer_10_out), .sel(Input_2));
  Multiplexer #(.width(4)) multiplexer_11 (
    .in0(multiplexer_5_out), .in1(Input_bus_17), .out(multiplexer_11_out), .sel(Input_2));
  Multiplexer #(.width(4)) multiplexer_12 (
    .in0(multiplexer_6_out), .in1(Input_bus_18), .out(multiplexer_12_out), .sel(Input_2));
  Multiplexer #(.width(4)) multiplexer_13 (
    .in0(multiplexer_7_out), .in1(Input_bus_19), .out(multiplexer_13_out), .sel(Input_3));
  Multiplexer #(.width(4)) multiplexer_14 (
    .in0(multiplexer_8_out), .in1(Input_bus_20), .out(multiplexer_14_out), .sel(Input_3));
  Multiplexer #(.width(4)) multiplexer_15 (
    .in0(multiplexer_9_out), .in1(Input_bus_21), .out(multiplexer_15_out), .sel(Input_3));
  Multiplexer #(.width(4)) multiplexer_16 (
    .in0(multiplexer_10_out), .in1(Input_bus_22), .out(multiplexer_16_out), .sel(Input_3));
  Multiplexer #(.width(4)) multiplexer_17 (
    .in0(multiplexer_11_out), .in1(Input_bus_23), .out(multiplexer_17_out), .sel(Input_3));
  Multiplexer #(.width(4)) multiplexer_18 (
    .in0(multiplexer_12_out), .in1(Input_bus_24), .out(multiplexer_18_out), .sel(Input_3));
  Multiplexer #(.width(4)) multiplexer_19 (
    .in0(multiplexer_13_out), .in1(Input_bus_25), .out(Output_bus_1), .sel(Input_4));
  Multiplexer #(.width(4)) multiplexer_20 (
    .in0(multiplexer_14_out), .in1(Input_bus_26), .out(Output_bus_2), .sel(Input_4));
  Multiplexer #(.width(4)) multiplexer_21 (
    .in0(multiplexer_15_out), .in1(Input_bus_27), .out(Output_bus_3), .sel(Input_4));
  Multiplexer #(.width(4)) multiplexer_22 (
    .in0(multiplexer_16_out), .in1(Input_bus_28), .out(Output_bus_4), .sel(Input_4));
  Multiplexer #(.width(4)) multiplexer_23 (
    .in0(multiplexer_17_out), .in1(Input_bus_29), .out(Output_bus_5), .sel(Input_4));
  Multiplexer #(.width(4)) multiplexer_24 (
    .in0(multiplexer_18_out), .in1(Input_bus_30), .out(Output_bus_6), .sel(Input_4));
endmodule

module Reset (
  input  [3:0] Input_bus_1,
  input  [3:0] Input_bus_2,
  input  [3:0] Input_bus_3,
  input  [3:0] Input_bus_4,
  input  [3:0] Input_bus_5,
  input  [3:0] Input_bus_6,
  input  Input_1,
  output Output_1
);

  wire and_1_out, and_2_out, and_3_out, and_4_out, and_5_out, and_6_out, and_7_out, and_8_out, and_9_out,
       and_10_out, and_11_out, and_12_out, and_13_out, and_14_out, clock_1_out, d_ff_1_q, not_1_out,
       not_2_out, not_3_out, not_4_out, not_5_out, not_6_out, not_7_out, not_8_out, not_9_out, not_10_out,
       not_11_out, not_12_out, not_13_out, not_14_out, not_15_out, not_16_out, not_17_out, not_18_out,
       not_19_out, not_20_out, not_21_out, not_22_out, not_23_out, not_24_out, not_25_out, not_26_out,
       not_27_out, not_28_out, not_29_out, not_30_out, not_31_out, not_32_out, not_33_out, not_34_out,
       not_35_out;

  not not_1 (not_1_out, Input_bus_1[1]);
  and and_1 (and_1_out, Input_bus_1[0], not_1_out, not_2_out, Input_bus_1[3]);
  not not_2 (not_2_out, Input_bus_1[2]);
  not not_3 (not_3_out, Input_bus_2[1]);
  and and_2 (and_2_out, Input_bus_2[0], not_3_out, Input_bus_2[2], not_4_out);
  not not_4 (not_4_out, Input_bus_2[3]);
  not not_5 (not_5_out, Input_bus_3[1]);
  and and_3 (and_3_out, Input_bus_3[0], not_5_out, not_6_out, Input_bus_3[3]);
  not not_6 (not_6_out, Input_bus_3[2]);
  not not_7 (not_7_out, Input_bus_4[1]);
  and and_4 (and_4_out, Input_bus_4[0], not_7_out, Input_bus_4[2], not_8_out);
  not not_8 (not_8_out, Input_bus_4[3]);
  and and_5 (and_5_out, Input_bus_5[0], Input_bus_5[1], not_9_out, not_10_out);
  not not_9 (not_9_out, Input_bus_5[2]);
  not not_10 (not_10_out, Input_bus_5[3]);
  not not_11 (not_11_out, Input_bus_6[0]);
  and and_6 (and_6_out, not_11_out, Input_bus_6[1], not_12_out, not_13_out);
  not not_12 (not_12_out, Input_bus_6[2]);
  not not_13 (not_13_out, Input_bus_6[3]);
  not not_14 (not_14_out, Input_bus_1[0]);
  not not_15 (not_15_out, Input_bus_1[1]);
  not not_16 (not_16_out, Input_bus_1[2]);
  not not_17 (not_17_out, Input_bus_1[3]);
  not not_18 (not_18_out, Input_bus_2[0]);
  not not_19 (not_19_out, Input_bus_2[1]);
  not not_20 (not_20_out, Input_bus_2[2]);
  not not_21 (not_21_out, Input_bus_2[3]);
  not not_22 (not_22_out, Input_bus_3[0]);
  not not_23 (not_23_out, Input_bus_3[1]);
  not not_24 (not_24_out, Input_bus_3[2]);
  not not_25 (not_25_out, Input_bus_3[3]);
  not not_26 (not_26_out, Input_bus_4[0]);
  not not_27 (not_27_out, Input_bus_4[1]);
  not not_28 (not_28_out, Input_bus_4[2]);
  not not_29 (not_29_out, Input_bus_4[3]);
  not not_30 (not_30_out, Input_bus_5[0]);
  not not_31 (not_31_out, Input_bus_5[1]);
  not not_32 (not_32_out, Input_bus_5[3]);
  not not_33 (not_33_out, Input_bus_6[0]);
  not not_34 (not_34_out, Input_bus_6[2]);
  not not_35 (not_35_out, Input_bus_6[3]);
  and and_7 (and_7_out, not_14_out, not_15_out, not_16_out, not_17_out);
  and and_8 (and_8_out, not_18_out, not_19_out, not_20_out, not_21_out);
  and and_9 (and_9_out, not_22_out, not_23_out, not_24_out, not_25_out);
  and and_10 (and_10_out, not_26_out, not_27_out, not_28_out, not_29_out);
  and and_11 (and_11_out, not_30_out, not_31_out, Input_bus_5[2], not_32_out);
  and and_12 (and_12_out, not_33_out, Input_bus_6[1], not_34_out, not_35_out);
  and and_13 (and_13_out, and_1_out, and_2_out, and_3_out, and_4_out, and_5_out, and_6_out);
  and and_14 (and_14_out, and_7_out, and_8_out, and_9_out, and_10_out, and_11_out, and_12_out);
  D_Flip_Flop d_ff_1 (.D(and_13_out), .clk(clock_1_out), .Q(d_ff_1_q), .reset(Input_1));  // open: Qn, preset
  Clock clock_1 (.out(clock_1_out));
  and and_15 (Output_1, d_ff_1_q, and_14_out);

  // Other names for the same wires on the sheet: RS = Input_1
endmodule

module Compteur9 (
  input  Input_1,
  input  Input_2,
  output [3:0] Output_bus_1,
  output Output_1
);

  wire and_1_out, and_2_out, and_3_out, and_4_out, and_5_out, and_6_out, and_7_out, and_8_out, and_9_out,
       and_10_out, and_11_out, and_12_out, and_13_out, and_14_out, C0, C1, C2, C3, clock_1_out, not_1_out,
       not_2_out, not_3_out, not_4_out, not_5_out, Retenue, UP;

  Montant Montant_1 (.Input_1(Input_1), .Input_2(Input_2), .Output_1(UP));
  Descendant Descendant_1 (.Input_1(Retenue), .Input_2(Input_2), .Output_1(Output_1));
  not not_1 (not_1_out, UP);
  not not_2 (not_2_out, C3);
  not not_3 (not_3_out, C2);
  not not_4 (not_4_out, C1);
  not not_5 (not_5_out, C0);
  and and_1 (and_1_out, not_1_out, C3, not_3_out, not_4_out);
  and and_2 (and_2_out, C3, not_3_out, not_4_out, not_5_out);
  and and_3 (and_3_out, UP, not_2_out, C2, C1, C0);
  and and_4 (and_4_out, not_1_out, not_2_out, C2);
  and and_5 (and_5_out, not_2_out, C2, not_4_out);
  and and_6 (and_6_out, not_2_out, C2, not_5_out);
  and and_7 (and_7_out, UP, not_2_out, not_3_out, C1, C0);
  and and_8 (and_8_out, not_1_out, not_2_out, C1);
  and and_9 (and_9_out, not_2_out, C1, not_5_out);
  and and_10 (and_10_out, UP, not_2_out, not_4_out, C0);
  and and_11 (and_11_out, not_1_out, not_2_out, C0);
  and and_12 (and_12_out, not_1_out, not_3_out, not_4_out, C0);
  and and_13 (and_13_out, UP, not_2_out, not_5_out);
  and and_14 (and_14_out, UP, not_3_out, not_4_out, not_5_out);
  or or_1 (Output_bus_1[3], and_1_out, and_2_out, and_3_out);
  or or_2 (Output_bus_1[2], and_4_out, and_5_out, and_6_out, and_7_out);
  or or_3 (Output_bus_1[1], and_8_out, and_9_out, and_10_out);
  or or_4 (Output_bus_1[0], and_11_out, and_12_out, and_13_out, and_14_out);
  D_Flip_Flop d_ff_1 (.D(Output_bus_1[3]), .clk(clock_1_out), .Q(C3), .reset(Input_2));  // open: Qn, preset
  Clock clock_1 (.out(clock_1_out));
  D_Flip_Flop d_ff_2 (.D(Output_bus_1[2]), .clk(clock_1_out), .Q(C2), .reset(Input_2));  // open: Qn, preset
  D_Flip_Flop d_ff_3 (.D(Output_bus_1[1]), .clk(clock_1_out), .Q(C1), .reset(Input_2));  // open: Qn, preset
  D_Flip_Flop d_ff_4 (.D(Output_bus_1[0]), .clk(clock_1_out), .Q(C0), .reset(Input_2));  // open: Qn, preset
  and and_15 (Retenue, Output_bus_1[0], ~Output_bus_1[1], ~Output_bus_1[2], Output_bus_1[3]);  // AND_Gate

  // Other names for the same wires on the sheet: CLICK = Input_1; D0 = Output_bus_1[0]; D1 = Output_bus_1[1];
  //   D2 = Output_bus_1[2]; D3 = Output_bus_1[3]; RST = Input_2
endmodule

module Compteur5 (
  input  Input_1,
  input  Input_2,
  output [3:0] Output_bus_1,
  output Output_1
);

  wire and_1_out, and_2_out, and_3_out, and_4_out, and_5_out, and_6_out, and_7_out, and_8_out, and_9_out,
       and_10_out, C0, C1, C2, C3, clock_1_out, not_1_out, not_2_out, not_3_out, not_4_out, not_5_out,
       Retenue, UP;

  Montant Montant_1 (.Input_1(Input_1), .Input_2(Input_2), .Output_1(UP));
  Descendant Descendant_1 (.Input_1(Retenue), .Input_2(Input_2), .Output_1(Output_1));
  not not_1 (not_1_out, UP);
  not not_2 (not_2_out, C3);
  not not_3 (not_3_out, C2);
  not not_4 (not_4_out, C1);
  not not_5 (not_5_out, C0);
  and and_1 (and_1_out, not_1_out, not_2_out, C2, not_4_out);
  and and_2 (and_2_out, not_2_out, C2, not_4_out, not_5_out);
  and and_3 (and_3_out, UP, not_2_out, not_3_out, C1, C0);
  and and_4 (and_4_out, not_1_out, not_2_out, not_3_out, C1);
  and and_5 (and_5_out, not_2_out, not_3_out, C1, not_5_out);
  and and_6 (and_6_out, UP, not_2_out, not_3_out, not_4_out, C0);
  and and_7 (and_7_out, not_1_out, not_2_out, not_3_out, C0);
  and and_8 (and_8_out, not_1_out, not_2_out, not_4_out, C0);
  and and_9 (and_9_out, UP, not_2_out, not_3_out, not_5_out);
  and and_10 (and_10_out, UP, not_2_out, not_4_out, not_5_out);
  or or_1 (Output_bus_1[2], and_1_out, and_2_out, and_3_out);
  or or_2 (Output_bus_1[1], and_4_out, and_5_out, and_6_out);
  or or_3 (Output_bus_1[0], and_7_out, and_8_out, and_9_out, and_10_out);
  D_Flip_Flop d_ff_1 (.D(1'b0), .clk(clock_1_out), .Q(C3), .reset(Input_2));  // open: Qn, preset
  Clock clock_1 (.out(clock_1_out));
  D_Flip_Flop d_ff_2 (.D(Output_bus_1[2]), .clk(clock_1_out), .Q(C2), .reset(Input_2));  // open: Qn, preset
  D_Flip_Flop d_ff_3 (.D(Output_bus_1[1]), .clk(clock_1_out), .Q(C1), .reset(Input_2));  // open: Qn, preset
  D_Flip_Flop d_ff_4 (.D(Output_bus_1[0]), .clk(clock_1_out), .Q(C0), .reset(Input_2));  // open: Qn, preset
  and and_11 (Retenue, Output_bus_1[0], ~Output_bus_1[1], Output_bus_1[2], ~1'b0);  // AND_Gate

  assign Output_bus_1[3] = 1'b0;

  // Other names for the same wires on the sheet: CLICK = Input_1; D0 = Output_bus_1[0]; D1 = Output_bus_1[1];
  //   D2 = Output_bus_1[2]; RST = Input_2
endmodule

module Compteur_9_SET (
  input  CLK,
  input  RST,
  input  Long_Press,
  input  [3:0] Binary_Entrance,
  output [3:0] Output_bus_1,
  output Output_1
);

  wire and_5_out, and_6_out, and_7_out, and_8_out, and_9_out, and_10_out, and_11_out, and_12_out, and_13_out,
       and_14_out, and_15_out, and_16_out, and_17_out, and_18_out, and_19_out, and_20_out, and_21_out,
       and_22_out, C0, C1, C2, C3, clock_1_out, LSB, MSB, not_1_out, not_2_out, not_3_out, not_4_out,
       not_5_out, or_5_out, or_6_out, or_7_out, or_8_out, Retenue, SSB, TSB, UP;

  Montant Montant_1 (.Input_1(CLK), .Input_2(RST), .Output_1(UP));
  Descendant Descendant_1 (.Input_1(Retenue), .Input_2(RST), .Output_1(Output_1));
  and and_1 (LSB, Binary_Entrance[0], Long_Press);
  and and_2 (SSB, Binary_Entrance[1], Long_Press);
  and and_3 (TSB, Binary_Entrance[2], Long_Press);
  and and_4 (MSB, Binary_Entrance[3], Long_Press);
  not not_1 (not_1_out, UP);
  not not_2 (not_2_out, C3);
  not not_3 (not_3_out, C2);
  not not_4 (not_4_out, C1);
  not not_5 (not_5_out, C0);
  and and_5 (and_5_out, not_1_out, C3, not_3_out, not_4_out);
  and and_6 (and_6_out, C3, not_3_out, not_4_out, not_5_out);
  and and_7 (and_7_out, UP, not_2_out, C2, C1, C0);
  and and_8 (and_8_out, not_1_out, not_2_out, C2);
  and and_9 (and_9_out, not_2_out, C2, not_4_out);
  and and_10 (and_10_out, not_2_out, C2, not_5_out);
  and and_11 (and_11_out, UP, not_2_out, not_3_out, C1, C0);
  and and_12 (and_12_out, not_1_out, not_2_out, C1);
  and and_13 (and_13_out, not_2_out, C1, not_5_out);
  and and_14 (and_14_out, UP, not_2_out, not_4_out, C0);
  and and_15 (and_15_out, not_1_out, not_2_out, C0);
  and and_16 (and_16_out, not_1_out, not_3_out, not_4_out, C0);
  and and_17 (and_17_out, UP, not_2_out, not_5_out);
  and and_18 (and_18_out, UP, not_3_out, not_4_out, not_5_out);
  or or_1 (Output_bus_1[3], and_5_out, and_6_out, and_7_out);
  or or_2 (Output_bus_1[2], and_8_out, and_9_out, and_10_out, and_11_out);
  or or_3 (Output_bus_1[1], and_12_out, and_13_out, and_14_out);
  or or_4 (Output_bus_1[0], and_15_out, and_16_out, and_17_out, and_18_out);
  Clock clock_1 (.out(clock_1_out));
  D_Flip_Flop d_ff_1 (.D(Output_bus_1[3]), .clk(clock_1_out), .Q(C3), .preset(MSB), .reset(or_5_out));  // open: Qn
  D_Flip_Flop d_ff_2 (.D(Output_bus_1[2]), .clk(clock_1_out), .Q(C2), .preset(TSB), .reset(or_6_out));  // open: Qn
  D_Flip_Flop d_ff_3 (.D(Output_bus_1[1]), .clk(clock_1_out), .Q(C1), .preset(SSB), .reset(or_7_out));  // open: Qn
  D_Flip_Flop d_ff_4 (.D(Output_bus_1[0]), .clk(clock_1_out), .Q(C0), .preset(LSB), .reset(or_8_out));  // open: Qn
  or or_5 (or_5_out, RST, and_19_out);
  and and_19 (and_19_out, Long_Press, ~MSB);  // AND_Gate
  or or_6 (or_6_out, RST, and_20_out);
  and and_20 (and_20_out, Long_Press, ~TSB);  // AND_Gate
  or or_7 (or_7_out, RST, and_21_out);
  and and_21 (and_21_out, Long_Press, ~SSB);  // AND_Gate
  or or_8 (or_8_out, RST, and_22_out);
  and and_22 (and_22_out, Long_Press, ~LSB);  // AND_Gate
  and and_23 (Retenue, Output_bus_1[0], ~Output_bus_1[1], ~Output_bus_1[2], Output_bus_1[3]);  // AND_Gate

  // Other names for the same wires on the sheet: CLICK = CLK; L_CLICK = Long_Press; D0 = Output_bus_1[0];
  //   D1 = Output_bus_1[1]; D2 = Output_bus_1[2]; D3 = Output_bus_1[3]
endmodule

module Compteur_5_SET (
  input  CLK,
  input  RST,
  input  Long_Press,
  input  [3:0] Binary_Entrance,
  output [3:0] Output_bus_1,
  output Output_1
);

  wire and_5_out, and_6_out, and_7_out, and_8_out, and_9_out, and_10_out, and_11_out, and_12_out, and_13_out,
       and_14_out, and_15_out, and_16_out, and_17_out, and_18_out, C0, C1, C2, C3, clock_1_out, LSB, MSB,
       not_1_out, not_2_out, not_3_out, not_4_out, not_5_out, or_4_out, or_5_out, or_6_out, or_7_out,
       Retenue, SSB, TSB, UP;

  Montant Montant_1 (.Input_1(CLK), .Input_2(RST), .Output_1(UP));
  Descendant Descendant_1 (.Input_1(Retenue), .Input_2(RST), .Output_1(Output_1));
  and and_1 (LSB, Binary_Entrance[0], Long_Press);
  and and_2 (SSB, Binary_Entrance[1], Long_Press);
  and and_3 (TSB, Binary_Entrance[2], Long_Press);
  and and_4 (MSB, Binary_Entrance[3], Long_Press);
  not not_1 (not_1_out, UP);
  not not_2 (not_2_out, C3);
  not not_3 (not_3_out, C2);
  not not_4 (not_4_out, C1);
  not not_5 (not_5_out, C0);
  and and_5 (and_5_out, not_1_out, not_2_out, C2, not_4_out);
  and and_6 (and_6_out, not_2_out, C2, not_4_out, not_5_out);
  and and_7 (and_7_out, UP, not_2_out, not_3_out, C1, C0);
  and and_8 (and_8_out, not_1_out, not_2_out, not_3_out, C1);
  and and_9 (and_9_out, not_2_out, not_3_out, C1, not_5_out);
  and and_10 (and_10_out, UP, not_2_out, not_3_out, not_4_out, C0);
  and and_11 (and_11_out, not_1_out, not_2_out, not_3_out, C0);
  and and_12 (and_12_out, not_1_out, not_2_out, not_4_out, C0);
  and and_13 (and_13_out, UP, not_2_out, not_3_out, not_5_out);
  and and_14 (and_14_out, UP, not_2_out, not_4_out, not_5_out);
  or or_1 (Output_bus_1[2], and_5_out, and_6_out, and_7_out);
  or or_2 (Output_bus_1[1], and_8_out, and_9_out, and_10_out);
  or or_3 (Output_bus_1[0], and_11_out, and_12_out, and_13_out, and_14_out);
  Clock clock_1 (.out(clock_1_out));
  D_Flip_Flop d_ff_1 (.D(1'b0), .clk(clock_1_out), .Q(C3), .preset(MSB), .reset(or_4_out));  // open: Qn
  D_Flip_Flop d_ff_2 (.D(Output_bus_1[2]), .clk(clock_1_out), .Q(C2), .preset(TSB), .reset(or_5_out));  // open: Qn
  D_Flip_Flop d_ff_3 (.D(Output_bus_1[1]), .clk(clock_1_out), .Q(C1), .preset(SSB), .reset(or_6_out));  // open: Qn
  D_Flip_Flop d_ff_4 (.D(Output_bus_1[0]), .clk(clock_1_out), .Q(C0), .preset(LSB), .reset(or_7_out));  // open: Qn
  or or_4 (or_4_out, RST, and_15_out);
  and and_15 (and_15_out, Long_Press, ~MSB);  // AND_Gate
  or or_5 (or_5_out, RST, and_16_out);
  and and_16 (and_16_out, Long_Press, ~TSB);  // AND_Gate
  or or_6 (or_6_out, RST, and_17_out);
  and and_17 (and_17_out, Long_Press, ~SSB);  // AND_Gate
  or or_7 (or_7_out, RST, and_18_out);
  and and_18 (and_18_out, Long_Press, ~LSB);  // AND_Gate
  and and_19 (Retenue, Output_bus_1[0], ~Output_bus_1[1], Output_bus_1[2], ~1'b0);  // AND_Gate

  assign Output_bus_1[3] = 1'b0;

  // Other names for the same wires on the sheet: CLICK = CLK; L_CLICK = Long_Press; D0 = Output_bus_1[0];
  //   D1 = Output_bus_1[1]; D2 = Output_bus_1[2]
endmodule

module Count_Setting_2 (
  input  Input_1,
  input  Input_2,
  input  Input_3,
  output [3:0] Output_bus_1
);

  wire and_1_out, and_4_out, and_5_out, and_6_out, and_7_out, and_8_out, B1, B2, B3, B4, clock_1_out,
       clock_2_out, d_ff_5_q, d_ff_5_qn, d_ff_6_q, not_1_out, not_2_out, not_3_out, not_4_out, not_5_out,
       not_6_out;

  Clock clock_1 (.out(clock_1_out));
  Clock clock_2 (.out(clock_2_out));
  D_Flip_Flop d_ff_1 (.D(Output_bus_1[3]), .clk(clock_1_out), .Q(B1), .reset(Input_3));  // open: Qn, preset
  D_Flip_Flop d_ff_2 (.D(Output_bus_1[2]), .clk(clock_1_out), .Q(B2), .reset(Input_3));  // open: Qn, preset
  D_Flip_Flop d_ff_3 (.D(Output_bus_1[1]), .clk(clock_1_out), .Q(B3), .reset(Input_3));  // open: Qn, preset
  D_Flip_Flop d_ff_4 (.D(Output_bus_1[0]), .clk(clock_1_out), .Q(B4), .reset(Input_3));  // open: Qn, preset
  D_Flip_Flop #(.trigger("falling")) d_ff_5 (
    .D(Input_1), .clk(clock_2_out), .Q(d_ff_5_q), .Qn(d_ff_5_qn));  // open: preset, reset
  D_Flip_Flop d_ff_6 (.D(d_ff_5_qn), .clk(clock_2_out), .Q(d_ff_6_q));  // open: Qn, preset, reset
  and and_1 (and_1_out, d_ff_5_q, d_ff_6_q);
  not not_1 (not_1_out, and_1_out);
  not not_2 (not_2_out, Input_2);
  not not_3 (not_3_out, B1);
  not not_4 (not_4_out, B2);
  not not_5 (not_5_out, B3);
  not not_6 (not_6_out, B4);
  and and_2 (Output_bus_1[3], not_1_out, not_2_out, B1);
  and and_3 (Output_bus_1[2], not_1_out, not_2_out, B2);
  and and_4 (and_4_out, not_1_out, not_2_out, B3);
  and and_5 (and_5_out, and_1_out, not_2_out, not_3_out, not_4_out, not_5_out, B4);
  and and_6 (and_6_out, not_1_out, not_2_out, B4);
  and and_7 (and_7_out, not_1_out, not_3_out, not_4_out, not_5_out, B4);
  and and_8 (and_8_out, and_1_out, not_3_out, not_4_out, not_5_out, not_6_out);
  or or_1 (Output_bus_1[1], and_4_out, and_5_out);
  or or_2 (Output_bus_1[0], and_6_out, and_7_out, and_8_out);

  // Other names for the same wires on the sheet: B = Input_2; CLICK = Input_1; B44 = Output_bus_1[0];
  //   B33 = Output_bus_1[1]; B22 = Output_bus_1[2]; B11 = Output_bus_1[3]; RS = Input_3
endmodule

module Count_Setting_4 (
  input  Input_1,
  input  Input_2,
  input  Input_3,
  output [3:0] Output_bus_1
);

  wire and_1_out, and_2_out, and_3_out, and_4_out, and_5_out, and_6_out, and_7_out, and_8_out, and_9_out,
       and_10_out, and_11_out, and_12_out, and_13_out, and_14_out, and_15_out, and_16_out, and_17_out,
       and_18_out, and_19_out, and_20_out, B1, B2, B3, B4, clock_1_out, clock_2_out, d_ff_5_q, d_ff_5_qn,
       d_ff_6_q, not_1_out, not_2_out, not_3_out, not_4_out, not_5_out, not_6_out;

  Clock clock_1 (.out(clock_1_out));
  D_Flip_Flop d_ff_1 (.D(Output_bus_1[3]), .clk(clock_1_out), .Q(B1), .reset(Input_3));  // open: Qn, preset
  D_Flip_Flop d_ff_2 (.D(Output_bus_1[2]), .clk(clock_1_out), .Q(B2), .reset(Input_3));  // open: Qn, preset
  D_Flip_Flop d_ff_3 (.D(Output_bus_1[1]), .clk(clock_1_out), .Q(B3), .reset(Input_3));  // open: Qn, preset
  D_Flip_Flop d_ff_4 (.D(Output_bus_1[0]), .clk(clock_1_out), .Q(B4), .reset(Input_3));  // open: Qn, preset
  D_Flip_Flop #(.trigger("falling")) d_ff_5 (
    .D(Input_1), .clk(clock_2_out), .Q(d_ff_5_q), .Qn(d_ff_5_qn));  // open: preset, reset
  Clock clock_2 (.out(clock_2_out));
  D_Flip_Flop d_ff_6 (.D(d_ff_5_qn), .clk(clock_2_out), .Q(d_ff_6_q));  // open: Qn, preset, reset
  and and_1 (and_1_out, d_ff_5_q, d_ff_6_q);
  not not_1 (not_1_out, and_1_out);
  not not_2 (not_2_out, Input_2);
  not not_3 (not_3_out, B1);
  not not_4 (not_4_out, B2);
  not not_5 (not_5_out, B3);
  not not_6 (not_6_out, B4);
  and and_2 (and_2_out, not_1_out, not_2_out, B1, not_4_out, not_5_out);
  and and_3 (and_3_out, not_2_out, B1, not_4_out, not_5_out, not_6_out);
  and and_4 (and_4_out, and_1_out, not_2_out, not_3_out, B2, B3, B4);
  and and_5 (and_5_out, not_1_out, not_2_out, not_3_out, B2);
  and and_6 (and_6_out, not_2_out, not_3_out, B2, not_5_out);
  and and_7 (and_7_out, not_2_out, not_3_out, B2, not_6_out);
  and and_8 (and_8_out, and_1_out, not_2_out, not_3_out, not_4_out, B3, B4);
  and and_9 (and_9_out, not_1_out, not_2_out, not_3_out, B3);
  and and_10 (and_10_out, not_1_out, not_3_out, not_4_out, B3);
  and and_11 (and_11_out, not_2_out, not_3_out, B3, not_6_out);
  and and_12 (and_12_out, not_3_out, not_4_out, B3, not_6_out);
  and and_13 (and_13_out, and_1_out, not_2_out, not_3_out, not_5_out, B4);
  and and_14 (and_14_out, and_1_out, not_3_out, not_4_out, not_5_out, B4);
  and and_15 (and_15_out, not_1_out, not_2_out, not_3_out, B4);
  and and_16 (and_16_out, not_1_out, not_2_out, not_4_out, not_5_out, B4);
  and and_17 (and_17_out, not_1_out, not_3_out, not_4_out, B4);
  and and_18 (and_18_out, and_1_out, not_2_out, not_3_out, not_6_out);
  and and_19 (and_19_out, and_1_out, not_2_out, not_4_out, not_5_out, not_6_out);
  and and_20 (and_20_out, and_1_out, not_3_out, not_4_out, not_6_out);
  or or_1 (Output_bus_1[3], and_2_out, and_3_out, and_4_out);
  or or_2 (Output_bus_1[2], and_5_out, and_6_out, and_7_out, and_8_out);
  or or_3 (Output_bus_1[1], and_9_out, and_10_out, and_11_out, and_12_out, and_13_out, and_14_out);
  or or_4 (Output_bus_1[0], and_15_out, and_16_out, and_17_out, and_18_out, and_19_out, and_20_out);

  // Other names for the same wires on the sheet: CLICK = Input_1; B44 = Output_bus_1[0]; B33 = Output_bus_1[1];
  //   B22 = Output_bus_1[2]; B11 = Output_bus_1[3]; RS = Input_3; Two = Input_2
endmodule

module Watch (
  input  CLOCK,
  input  RST,
  output [3:0] Output_bus_1,
  output [3:0] Output_bus_2,
  output [3:0] Output_bus_3,
  output [3:0] Output_bus_4,
  output [3:0] Output_bus_5,
  output [3:0] Output_bus_6
);

  wire Compteur5_1_output_1, Compteur5_2_output_1, Compteur9_1_output_1, Compteur9_2_output_1,
       Compteur9_3_output_1, COPY, DOWN;

  Compteur9 Compteur9_1 (.Input_1(CLOCK), .Input_2(COPY), .Output_bus_1(Output_bus_6), .Output_1(Compteur9_1_output_1));
  or or_1 (COPY, RST, DOWN);
  Compteur5 Compteur5_1 (
    .Input_1(Compteur9_1_output_1), .Input_2(COPY), .Output_bus_1(Output_bus_5),
    .Output_1(Compteur5_1_output_1));
  Reset Reset_1 (
    .Input_bus_1(Output_bus_6), .Input_bus_2(Output_bus_5), .Input_bus_3(Output_bus_4),
    .Input_bus_4(Output_bus_3), .Input_bus_5(Output_bus_2), .Input_bus_6(Output_bus_1), .Input_1(RST),
    .Output_1(DOWN));
  Compteur9 Compteur9_2 (
    .Input_1(Compteur5_1_output_1), .Input_2(COPY), .Output_bus_1(Output_bus_4),
    .Output_1(Compteur9_2_output_1));
  Compteur5 Compteur5_2 (
    .Input_1(Compteur9_2_output_1), .Input_2(COPY), .Output_bus_1(Output_bus_3),
    .Output_1(Compteur5_2_output_1));
  Compteur9 Compteur9_3 (
    .Input_1(Compteur5_2_output_1), .Input_2(COPY), .Output_bus_1(Output_bus_2),
    .Output_1(Compteur9_3_output_1));
  Compteur9 Compteur9_4 (
    .Input_1(Compteur9_3_output_1), .Input_2(COPY), .Output_bus_1(Output_bus_1));  // open: Output_1

  // Other names for the same wires on the sheet: H_1[3:0] = Output_bus_1; H_2[3:0] = Output_bus_2;
  //   M_1[3:0] = Output_bus_3; M_2[3:0] = Output_bus_4; S_1[3:0] = Output_bus_5; S_2[3:0] = Output_bus_6
endmodule

module Watch_test (
  input  CLOCK,
  input  RST,
  input  Long_Press,
  input  [23:0] Binary_Entrance,
  output [3:0] Output_bus_1,
  output [3:0] Output_bus_2,
  output [3:0] Output_bus_3,
  output [3:0] Output_bus_4,
  output [3:0] Output_bus_5,
  output [3:0] Output_bus_6
);

  wire Compteur_5_SET_1_output_1, Compteur_5_SET_2_output_1, Compteur_9_SET_1_output_1,
       Compteur_9_SET_2_output_1, Compteur_9_SET_3_output_1, COPY, DOWN;

  Compteur_9_SET Compteur_9_SET_1 (
    .CLK(CLOCK), .RST(COPY), .Long_Press(Long_Press), .Binary_Entrance(Binary_Entrance[23:20]),
    .Output_bus_1(Output_bus_6), .Output_1(Compteur_9_SET_1_output_1));
  or or_1 (COPY, RST, DOWN);
  Compteur_5_SET Compteur_5_SET_1 (
    .CLK(Compteur_9_SET_1_output_1), .RST(COPY), .Long_Press(Long_Press),
    .Binary_Entrance(Binary_Entrance[19:16]), .Output_bus_1(Output_bus_5),
    .Output_1(Compteur_5_SET_1_output_1));
  Compteur_9_SET Compteur_9_SET_2 (
    .CLK(Compteur_5_SET_1_output_1), .RST(COPY), .Long_Press(Long_Press),
    .Binary_Entrance(Binary_Entrance[15:12]), .Output_bus_1(Output_bus_4),
    .Output_1(Compteur_9_SET_2_output_1));
  Reset Reset_1 (
    .Input_bus_1(Output_bus_6), .Input_bus_2(Output_bus_5), .Input_bus_3(Output_bus_4),
    .Input_bus_4(Output_bus_3), .Input_bus_5(Output_bus_2), .Input_bus_6(Output_bus_1), .Input_1(RST),
    .Output_1(DOWN));
  Compteur_5_SET Compteur_5_SET_2 (
    .CLK(Compteur_9_SET_2_output_1), .RST(COPY), .Long_Press(Long_Press),
    .Binary_Entrance(Binary_Entrance[11:8]), .Output_bus_1(Output_bus_3), .Output_1(Compteur_5_SET_2_output_1));
  Compteur_9_SET Compteur_9_SET_3 (
    .CLK(Compteur_5_SET_2_output_1), .RST(COPY), .Long_Press(Long_Press),
    .Binary_Entrance(Binary_Entrance[7:4]), .Output_bus_1(Output_bus_2), .Output_1(Compteur_9_SET_3_output_1));
  Compteur_5_SET Compteur_5_SET_3 (
    .CLK(Compteur_9_SET_3_output_1), .RST(COPY), .Long_Press(Long_Press),
    .Binary_Entrance(Binary_Entrance[3:0]), .Output_bus_1(Output_bus_1));  // open: Output_1

  // Other names for the same wires on the sheet: H_11[3:0] = Binary_Entrance[3:0]; H_22[3:0] = Binary_Entrance[7:4];
  //   M_11[3:0] = Binary_Entrance[11:8]; M_22[3:0] = Binary_Entrance[15:12]; S_11[3:0] = Binary_Entrance[19:16];
  //   S_22[3:0] = Binary_Entrance[23:20]; H_1[3:0] = Output_bus_1; H_2[3:0] = Output_bus_2; LP = Long_Press;
  //   M_1[3:0] = Output_bus_3; M_2[3:0] = Output_bus_4; S_1[3:0] = Output_bus_5; S_2[3:0] = Output_bus_6
endmodule

module Trans_Chrono (
  input  ENTER,
  input  A,
  input  B,
  input  RST,
  output ENABLE,
  output On_Off
);

  wire A1, A2, A_t, and_5_out, and_6_out, and_7_out, and_8_out, and_9_out, and_10_out, B_t, clock_1_out,
       clock_2_out, clock_3_out, clock_4_out, clock_5_out, clock_6_out, d_ff_1_q, d_ff_1_qn, d_ff_2_q,
       d_ff_2_qn, d_ff_3_q, d_ff_3_qn, d_ff_4_q, d_ff_4_qn, d_ff_5_q, d_ff_6_q, d_ff_7_q, d_ff_8_q, E1,
       ENTER_t, not_1_out, not_2_out, not_3_out, not_4_out, not_5_out, not_6_out, RST_t;

  D_Flip_Flop #(.trigger("falling")) d_ff_1 (
    .D(ENTER), .clk(clock_1_out), .Q(d_ff_1_q), .Qn(d_ff_1_qn));  // open: preset, reset
  Clock clock_1 (.out(clock_1_out));
  D_Flip_Flop #(.trigger("falling")) d_ff_2 (
    .D(A), .clk(clock_2_out), .Q(d_ff_2_q), .Qn(d_ff_2_qn));  // open: preset, reset
  Clock clock_2 (.out(clock_2_out));
  D_Flip_Flop #(.trigger("falling")) d_ff_3 (
    .D(B), .clk(clock_3_out), .Q(d_ff_3_q), .Qn(d_ff_3_qn));  // open: preset, reset
  Clock clock_3 (.out(clock_3_out));
  D_Flip_Flop #(.trigger("falling")) d_ff_4 (
    .D(RST), .clk(clock_4_out), .Q(d_ff_4_q), .Qn(d_ff_4_qn));  // open: preset, reset
  Clock clock_4 (.out(clock_4_out));
  Clock clock_5 (.out(clock_5_out));
  Clock clock_6 (.out(clock_6_out));
  D_Flip_Flop d_ff_5 (.D(d_ff_1_qn), .clk(clock_1_out), .Q(d_ff_5_q));  // open: Qn, preset, reset
  D_Flip_Flop d_ff_6 (.D(d_ff_2_qn), .clk(clock_2_out), .Q(d_ff_6_q));  // open: Qn, preset, reset
  D_Flip_Flop d_ff_7 (.D(d_ff_3_qn), .clk(clock_3_out), .Q(d_ff_7_q));  // open: Qn, preset, reset
  D_Flip_Flop d_ff_8 (.D(d_ff_4_qn), .clk(clock_4_out), .Q(d_ff_8_q));  // open: Qn, preset, reset
  D_Flip_Flop d_ff_9 (.D(On_Off), .clk(clock_5_out), .Q(E1));  // open: Qn, preset, reset
  D_Flip_Flop d_ff_10 (.D(A2), .clk(clock_6_out), .Q(A1));  // open: Qn, preset, reset
  and and_1 (ENTER_t, d_ff_1_q, d_ff_5_q);
  and and_2 (A_t, d_ff_2_q, d_ff_6_q);
  and and_3 (B_t, d_ff_3_q, d_ff_7_q);
  and and_4 (RST_t, d_ff_4_q, d_ff_8_q);
  not not_1 (not_1_out, ENTER_t);
  not not_2 (not_2_out, E1);
  not not_3 (not_3_out, A_t);
  not not_4 (not_4_out, A1);
  not not_5 (not_5_out, B_t);
  not not_6 (not_6_out, RST_t);
  and and_5 (and_5_out, not_1_out, E1, not_6_out);
  and and_6 (and_6_out, ENTER_t, not_2_out, not_6_out);
  and and_7 (and_7_out, not_1_out, E1, not_3_out, A1, not_5_out, not_6_out);
  and and_8 (and_8_out, not_1_out, E1, A_t, not_4_out, not_5_out, not_6_out);
  and and_9 (and_9_out, ENTER_t, not_2_out, not_3_out, A1, not_5_out, not_6_out);
  and and_10 (and_10_out, ENTER_t, not_2_out, A_t, not_4_out, not_5_out, not_6_out);
  or or_1 (On_Off, and_5_out, and_6_out);
  or or_2 (A2, and_7_out, and_8_out, and_9_out, and_10_out);
  and and_11 (ENABLE, On_Off, A2);

  // Other names for the same wires on the sheet: E2 = On_Off
endmodule

module Chrono (
  input  ENTER,
  input  A,
  input  B,
  input  RST_G,
  output [3:0] Output_bus_1,
  output [3:0] Output_bus_2,
  output [3:0] Output_bus_3,
  output [3:0] Output_bus_4,
  output [3:0] Output_bus_5,
  output [3:0] Output_bus_6,
  output On_Off
);

  wire clock_1_out, ENABLE, multiplexer_1_out, or_1_out;

  Multiplexer multiplexer_1 (.in0(1'b0), .in1(clock_1_out), .out(multiplexer_1_out), .sel(ENABLE));
  Clock #(.highDuration(17000), .lowDuration(17000)) clock_1 (.out(clock_1_out));
  or or_1 (or_1_out, B, RST_G);
  Trans_Chrono Trans_Chrono_1 (.ENTER(ENTER), .A(A), .B(B), .RST(RST_G), .ENABLE(ENABLE), .On_Off(On_Off));
  Watch Watch_1 (
    .CLOCK(multiplexer_1_out), .RST(or_1_out), .Output_bus_1(Output_bus_1), .Output_bus_2(Output_bus_2),
    .Output_bus_3(Output_bus_3), .Output_bus_4(Output_bus_4), .Output_bus_5(Output_bus_5),
    .Output_bus_6(Output_bus_6));

  // Other names for the same wires on the sheet: RST = RST_G
endmodule

module Setting (
  input  ENTER,
  input  A,
  input  B,
  input  DIP_1,
  input  DIP_2,
  input  DIP_3,
  input  RST,
  output [3:0] Output_bus_1,
  output [3:0] Output_bus_2,
  output [3:0] Output_bus_3,
  output [3:0] Output_bus_4,
  output [3:0] Output_bus_5,
  output [3:0] Output_bus_6
);

  wire and_1_out, and_2_out, and_3_out, multiplexer_1_out, multiplexer_2_out, multiplexer_3_out,
       multiplexer_4_out, multiplexer_5_out, multiplexer_6_out;

  and and_1 (and_1_out, ENTER, DIP_1);
  and and_2 (and_2_out, ENTER, DIP_2);
  and and_3 (and_3_out, ENTER, DIP_3);
  Multiplexer multiplexer_1 (.in0(1'b0), .in1(A), .out(multiplexer_1_out), .sel(and_1_out));
  Multiplexer multiplexer_2 (.in0(1'b0), .in1(B), .out(multiplexer_2_out), .sel(and_1_out));
  Multiplexer multiplexer_3 (.in0(1'b0), .in1(A), .out(multiplexer_3_out), .sel(and_2_out));
  Multiplexer multiplexer_4 (.in0(1'b0), .in1(B), .out(multiplexer_4_out), .sel(and_2_out));
  Multiplexer multiplexer_5 (.in0(1'b0), .in1(A), .out(multiplexer_5_out), .sel(and_3_out));
  Multiplexer multiplexer_6 (.in0(1'b0), .in1(B), .out(multiplexer_6_out), .sel(and_3_out));
  Set_Hre Set_Hre_1 (.A(multiplexer_1_out), .B(multiplexer_2_out), .RST(RST), .H_1(Output_bus_1), .H_2(Output_bus_2));
  Set_Min_Sec Set_Min_Sec_1 (
    .A(multiplexer_3_out), .B(multiplexer_4_out), .RST(RST), .M_S_1(Output_bus_3), .M_S_2(Output_bus_4));
  Set_Min_Sec Set_Min_Sec_2 (
    .A(multiplexer_5_out), .B(multiplexer_6_out), .RST(RST), .M_S_1(Output_bus_5), .M_S_2(Output_bus_6));
endmodule

module Set_Hre (
  input  A,
  input  B,
  input  RST,
  output [3:0] H_1,
  output [3:0] H_2
);

  wire and_2_out, and_3_out, and_4_out, and_5_out, and_6_out, and_7_out, ENABLE_1, Two;

  and and_1 (Two, ~H_1[0], H_1[1], ~H_1[2], ~H_1[3]);  // AND_Gate
  and and_2 (and_2_out, ~H_2[0], ~H_2[1], H_2[2], ~H_2[3]);  // AND_Gate
  and and_3 (and_3_out, ~H_2[0], H_2[1], H_2[2], ~H_2[3]);  // AND_Gate
  and and_4 (and_4_out, ~H_2[0], ~H_2[1], ~H_2[2], H_2[3]);  // AND_Gate
  Count_Setting_2 Count_Setting_2_1 (.Input_1(A), .Input_2(ENABLE_1), .Input_3(RST), .Output_bus_1(H_1));
  Count_Setting_4 Count_Setting_4_1 (.Input_1(B), .Input_2(Two), .Input_3(RST), .Output_bus_1(H_2));
  and and_5 (and_5_out, H_2[0], ~H_2[1], H_2[2], ~H_2[3]);  // AND_Gate
  and and_6 (and_6_out, H_2[0], H_2[1], H_2[2], ~H_2[3]);  // AND_Gate
  and and_7 (and_7_out, H_2[0], ~H_2[1], ~H_2[2], H_2[3]);  // AND_Gate
  or or_1 (ENABLE_1, and_2_out, and_5_out, and_3_out, and_6_out, and_4_out, and_7_out);

  // Other names for the same wires on the sheet: RST_1 = RST
endmodule

module Set_Min_Sec (
  input  A,
  input  B,
  input  RST,
  output [3:0] M_S_1,
  output [3:0] M_S_2
);

  Compteur5 Compteur5_1 (.Input_1(A), .Input_2(RST), .Output_bus_1(M_S_1));  // open: Output_1
  Compteur9 Compteur9_1 (.Input_1(B), .Input_2(RST), .Output_bus_1(M_S_2));  // open: Output_1
endmodule

module Alarm (
  input  [23:0] Heure_Courante,
  input  [23:0] Heure_Reveil,
  input  long_press,
  input  Stop,
  input  Reset_alarm,
  output S
);

  wire and_1_out, and_2_out, and_3_out, and_4_out, not_1_out, not_2_out, not_3_out, not_4_out, not_5_out,
       not_6_out, or_1_out, or_2_out, or_3_out, or_4_out, or_5_out, or_6_out;
  wire [3:0] Soustracteur_1_s, Soustracteur_2_s, Soustracteur_3_s, Soustracteur_4_s, Soustracteur_5_s,
       Soustracteur_6_s;

  Soustracteur Soustracteur_1 (
    .A(Heure_Reveil[3:0]), .B(Heure_Courante[3:0]), .S(Soustracteur_1_s));  // open: over_in, over_out
  Soustracteur Soustracteur_2 (
    .A(Heure_Reveil[7:4]), .B(Heure_Courante[7:4]), .S(Soustracteur_2_s));  // open: over_in, over_out
  Soustracteur Soustracteur_3 (
    .A(Heure_Reveil[11:8]), .B(Heure_Courante[11:8]), .S(Soustracteur_3_s));  // open: over_in, over_out
  Soustracteur Soustracteur_4 (
    .A(Heure_Reveil[15:12]), .B(Heure_Courante[15:12]), .S(Soustracteur_4_s));  // open: over_in, over_out
  Soustracteur Soustracteur_5 (
    .A(Heure_Reveil[19:16]), .B(Heure_Courante[19:16]), .S(Soustracteur_5_s));  // open: over_in, over_out
  Soustracteur Soustracteur_6 (
    .A(Heure_Reveil[23:20]), .B(Heure_Courante[23:20]), .S(Soustracteur_6_s));  // open: over_in, over_out
  or or_1 (or_1_out, Soustracteur_1_s[0], Soustracteur_1_s[1], Soustracteur_1_s[2], Soustracteur_1_s[3]);
  or or_2 (or_2_out, Soustracteur_2_s[0], Soustracteur_2_s[1], Soustracteur_2_s[2], Soustracteur_2_s[3]);
  or or_3 (or_3_out, Soustracteur_3_s[0], Soustracteur_3_s[1], Soustracteur_3_s[2], Soustracteur_3_s[3]);
  or or_4 (or_4_out, Soustracteur_4_s[0], Soustracteur_4_s[1], Soustracteur_4_s[2], Soustracteur_4_s[3]);
  or or_5 (or_5_out, Soustracteur_5_s[0], Soustracteur_5_s[1], Soustracteur_5_s[2], Soustracteur_5_s[3]);
  or or_6 (or_6_out, Soustracteur_6_s[0], Soustracteur_6_s[1], Soustracteur_6_s[2], Soustracteur_6_s[3]);
  not not_1 (not_1_out, or_1_out);
  not not_2 (not_2_out, or_2_out);
  not not_3 (not_3_out, or_3_out);
  not not_4 (not_4_out, or_4_out);
  not not_5 (not_5_out, or_5_out);
  not not_6 (not_6_out, or_6_out);
  and and_1 (and_1_out, not_1_out, not_2_out);
  and and_2 (and_2_out, not_3_out, not_4_out);
  and and_3 (and_3_out, not_5_out, not_6_out);
  and and_4 (and_4_out, and_1_out, and_2_out, and_3_out);
  Control_Alarm ggg_1 (.CLICK(long_press), .Soustracteur(and_4_out), .Stop(Stop), .RST(Reset_alarm), .S(S));

  // Other names for the same wires on the sheet: CLICK = long_press; RST = Reset_alarm
endmodule

module Soustracteur (
  input  over_in,
  input  [3:0] A,
  input  [3:0] B,
  output [3:0] S,
  output over_out
);

  wire subtractor_1_bout, subtractor_2_bout, subtractor_3_bout;

  Subtractor #(.width(1)) subtractor_1 (.a(A[0]), .b(B[0]), .out(S[0]), .bin(over_in), .bout(subtractor_1_bout));
  Subtractor #(.width(1)) subtractor_2 (
    .a(A[1]), .b(B[1]), .out(S[1]), .bin(subtractor_1_bout), .bout(subtractor_2_bout));
  Subtractor #(.width(1)) subtractor_3 (
    .a(A[2]), .b(B[2]), .out(S[2]), .bin(subtractor_2_bout), .bout(subtractor_3_bout));
  Subtractor #(.width(1)) subtractor_4 (.a(A[3]), .b(B[3]), .out(S[3]), .bin(subtractor_3_bout), .bout(over_out));
endmodule

module Control_Alarm (
  input  CLICK,
  input  Soustracteur,
  input  Stop,
  input  RST,
  output S
);

  wire and_2_out, and_3_out, and_4_out, and_5_out, C_1, C_2, clock_1_out, clock_2_out, Montant_1_output_1,
       Montant_2_output_1, not_1_out, On_Off_1, On_Off_2;

  D_Flip_Flop d_ff_1 (.D(On_Off_2), .clk(clock_1_out), .Q(On_Off_1), .reset(RST));  // open: Qn, preset
  Clock clock_1 (.out(clock_1_out));
  D_Flip_Flop d_ff_2 (.D(C_2), .clk(clock_2_out), .Q(C_1), .reset(RST));  // open: Qn, preset
  Clock clock_2 (.out(clock_2_out));
  Montant Montant_1 (.Input_1(CLICK), .Output_1(Montant_1_output_1));  // open: Input_2
  Montant Montant_2 (.Input_1(Soustracteur), .Output_1(Montant_2_output_1));  // open: Input_2
  and and_1 (S, On_Off_2, C_2);
  not not_1 (not_1_out, Stop);
  and and_2 (and_2_out, On_Off_1, not_1_out);
  and and_3 (and_3_out, Montant_1_output_1, not_1_out);
  and and_4 (and_4_out, C_1, not_1_out);
  and and_5 (and_5_out, Montant_2_output_1, not_1_out);
  or or_1 (On_Off_2, and_2_out, and_3_out);
  or or_2 (C_2, and_4_out, and_5_out);
endmodule

module Count_Min_9_One (
  input  CLICK,
  input  SET,
  input  FIN,
  input  RST,
  input  [3:0] Binary_Entrance,
  output RETENUE,
  output RETENUE_END,
  output [3:0] S
);

  wire and_1_out, and_2_out, and_3_out, and_4_out, and_10_out, and_11_out, and_12_out, and_13_out,
       and_14_out, and_15_out, and_16_out, and_17_out, and_18_out, and_19_out, and_20_out, and_21_out,
       and_22_out, and_23_out, B1, B2, B3, B4, CLICK_1, clock_1_out, clock_2_out, d_ff_1_q, d_ff_1_qn,
       d_ff_6_q, LSB, MSB, not_1_out, not_2_out, not_3_out, not_4_out, not_5_out, not_6_out, or_1_out,
       or_2_out, or_3_out, or_4_out, SSB, TSB;

  Clock clock_1 (.out(clock_1_out));
  D_Flip_Flop #(.trigger("falling")) d_ff_1 (
    .D(CLICK), .clk(clock_2_out), .Q(d_ff_1_q), .Qn(d_ff_1_qn));  // open: preset, reset
  Clock clock_2 (.out(clock_2_out));
  D_Flip_Flop d_ff_2 (.D(S[3]), .clk(clock_1_out), .Q(B1), .preset(MSB), .reset(or_1_out));  // open: Qn
  D_Flip_Flop d_ff_3 (.D(S[2]), .clk(clock_1_out), .Q(B2), .preset(TSB), .reset(or_2_out));  // open: Qn
  D_Flip_Flop d_ff_4 (.D(S[1]), .clk(clock_1_out), .Q(B3), .preset(SSB), .reset(or_3_out));  // open: Qn
  D_Flip_Flop d_ff_5 (.D(S[0]), .clk(clock_1_out), .Q(B4), .preset(LSB), .reset(or_4_out));  // open: Qn
  D_Flip_Flop d_ff_6 (.D(d_ff_1_qn), .clk(clock_2_out), .Q(d_ff_6_q));  // open: Qn, preset, reset
  or or_1 (or_1_out, RST, and_1_out);
  and and_1 (and_1_out, SET, ~MSB);  // AND_Gate
  or or_2 (or_2_out, RST, and_2_out);
  and and_2 (and_2_out, SET, ~TSB);  // AND_Gate
  or or_3 (or_3_out, RST, and_3_out);
  and and_3 (and_3_out, SET, ~SSB);  // AND_Gate
  or or_4 (or_4_out, RST, and_4_out);
  and and_4 (and_4_out, SET, ~LSB);  // AND_Gate
  and and_5 (CLICK_1, d_ff_1_q, d_ff_6_q);
  and and_6 (LSB, Binary_Entrance[0], SET);
  and and_7 (SSB, Binary_Entrance[1], SET);
  and and_8 (TSB, Binary_Entrance[2], SET);
  and and_9 (MSB, Binary_Entrance[3], SET);
  not not_1 (not_1_out, CLICK_1);
  not not_2 (not_2_out, FIN);
  not not_3 (not_3_out, B1);
  not not_4 (not_4_out, B2);
  not not_5 (not_5_out, B3);
  not not_6 (not_6_out, B4);
  and and_10 (and_10_out, not_1_out, not_2_out, B1);
  and and_11 (and_11_out, not_2_out, B1, not_4_out, not_5_out, B4);
  and and_12 (and_12_out, CLICK_1, not_2_out, not_3_out, not_4_out, not_5_out, not_6_out);
  and and_13 (and_13_out, not_1_out, not_2_out, B2);
  and and_14 (and_14_out, not_2_out, not_3_out, B2, B4);
  and and_15 (and_15_out, not_2_out, not_3_out, B2, B3);
  and and_16 (and_16_out, CLICK_1, not_2_out, B1, not_4_out, not_5_out, not_6_out);
  and and_17 (and_17_out, not_1_out, not_2_out, B3);
  and and_18 (and_18_out, not_2_out, not_3_out, B3, B4);
  and and_19 (and_19_out, CLICK_1, not_2_out, not_3_out, B2, not_5_out, not_6_out);
  and and_20 (and_20_out, CLICK_1, not_2_out, B1, not_4_out, not_5_out, not_6_out);
  and and_21 (and_21_out, not_1_out, not_2_out, B4);
  and and_22 (and_22_out, CLICK_1, not_2_out, not_3_out, not_6_out);
  and and_23 (and_23_out, CLICK_1, not_2_out, not_4_out, not_5_out, not_6_out);
  and and_24 (RETENUE, CLICK_1, not_2_out, not_3_out, not_4_out, not_5_out, not_6_out);
  and and_25 (RETENUE_END, CLICK_1, not_2_out, not_3_out, not_4_out, not_5_out, B4);
  or or_5 (S[3], and_10_out, and_11_out, and_12_out);
  or or_6 (S[2], and_13_out, and_14_out, and_15_out, and_16_out);
  or or_7 (S[1], and_17_out, and_18_out, and_19_out, and_20_out);
  or or_8 (S[0], and_21_out, and_22_out, and_23_out);

  // Other names for the same wires on the sheet: Binary[3:0] = Binary_Entrance; D4 = S[0]; D3 = S[1]; D2 = S[2];
  //   D1 = S[3]
endmodule

module Count_Min_9 (
  input  CLICK,
  input  SET,
  input  FIN,
  input  RST,
  input  [3:0] Binary_Entrance,
  output RETENUE,
  output [3:0] S
);

  wire and_1_out, and_2_out, and_3_out, and_4_out, and_9_out, and_10_out, and_11_out, and_12_out, and_13_out,
       and_14_out, and_15_out, and_16_out, and_17_out, and_18_out, and_19_out, and_20_out, and_21_out,
       and_22_out, B1, B2, B3, B4, clock_1_out, LSB, MSB, not_1_out, not_2_out, not_3_out, not_4_out,
       not_5_out, not_6_out, or_1_out, or_2_out, or_3_out, or_4_out, SSB, TSB;

  Clock clock_1 (.out(clock_1_out));
  D_Flip_Flop d_ff_1 (.D(S[3]), .clk(clock_1_out), .Q(B1), .preset(MSB), .reset(or_1_out));  // open: Qn
  D_Flip_Flop d_ff_2 (.D(S[2]), .clk(clock_1_out), .Q(B2), .preset(TSB), .reset(or_2_out));  // open: Qn
  D_Flip_Flop d_ff_3 (.D(S[1]), .clk(clock_1_out), .Q(B3), .preset(SSB), .reset(or_3_out));  // open: Qn
  D_Flip_Flop d_ff_4 (.D(S[0]), .clk(clock_1_out), .Q(B4), .preset(LSB), .reset(or_4_out));  // open: Qn
  or or_1 (or_1_out, RST, and_1_out);
  and and_1 (and_1_out, SET, ~MSB);  // AND_Gate
  or or_2 (or_2_out, RST, and_2_out);
  and and_2 (and_2_out, SET, ~TSB);  // AND_Gate
  or or_3 (or_3_out, RST, and_3_out);
  and and_3 (and_3_out, SET, ~SSB);  // AND_Gate
  or or_4 (or_4_out, RST, and_4_out);
  and and_4 (and_4_out, SET, ~LSB);  // AND_Gate
  and and_5 (LSB, Binary_Entrance[0], SET);
  and and_6 (SSB, Binary_Entrance[1], SET);
  and and_7 (TSB, Binary_Entrance[2], SET);
  and and_8 (MSB, Binary_Entrance[3], SET);
  not not_1 (not_1_out, CLICK);
  not not_2 (not_2_out, FIN);
  not not_3 (not_3_out, B1);
  not not_4 (not_4_out, B2);
  not not_5 (not_5_out, B3);
  not not_6 (not_6_out, B4);
  and and_9 (and_9_out, not_1_out, not_2_out, B1);
  and and_10 (and_10_out, not_2_out, B1, not_4_out, not_5_out, B4);
  and and_11 (and_11_out, CLICK, not_2_out, not_3_out, not_4_out, not_5_out, not_6_out);
  and and_12 (and_12_out, not_1_out, not_2_out, B2);
  and and_13 (and_13_out, not_2_out, not_3_out, B2, B4);
  and and_14 (and_14_out, not_2_out, not_3_out, B2, B3);
  and and_15 (and_15_out, CLICK, not_2_out, B1, not_4_out, not_5_out, not_6_out);
  and and_16 (and_16_out, not_1_out, not_2_out, B3);
  and and_17 (and_17_out, not_2_out, not_3_out, B3, B4);
  and and_18 (and_18_out, CLICK, not_2_out, not_3_out, B2, not_5_out, not_6_out);
  and and_19 (and_19_out, CLICK, not_2_out, B1, not_4_out, not_5_out, not_6_out);
  and and_20 (and_20_out, not_1_out, not_2_out, B4);
  and and_21 (and_21_out, CLICK, not_2_out, not_3_out, not_6_out);
  and and_22 (and_22_out, CLICK, not_2_out, not_4_out, not_5_out, not_6_out);
  and and_23 (RETENUE, CLICK, not_2_out, not_3_out, not_4_out, not_5_out, not_6_out);
  or or_5 (S[3], and_9_out, and_10_out, and_11_out);
  or or_6 (S[2], and_12_out, and_13_out, and_14_out, and_15_out);
  or or_7 (S[1], and_16_out, and_17_out, and_18_out, and_19_out);
  or or_8 (S[0], and_20_out, and_21_out, and_22_out);

  // Other names for the same wires on the sheet: Binary[3:0] = Binary_Entrance; D4 = S[0]; D3 = S[1]; D2 = S[2];
  //   D1 = S[3]
endmodule

module Count_Min_5 (
  input  CLICK,
  input  SET,
  input  FIN,
  input  RST,
  input  [3:0] Binary_Entrance,
  output RETENUE,
  output [3:0] Output_bus_1
);

  wire and_1_out, and_2_out, and_3_out, and_4_out, and_10_out, and_11_out, and_12_out, and_13_out,
       and_14_out, and_15_out, and_16_out, and_17_out, and_18_out, B1, B2, B3, B4, clock_1_out, LSB, MSB,
       not_1_out, not_2_out, not_3_out, not_4_out, not_5_out, not_6_out, or_1_out, or_2_out, or_3_out,
       or_4_out, SSB, TSB;

  Clock clock_1 (.out(clock_1_out));
  D_Flip_Flop d_ff_1 (.D(Output_bus_1[3]), .clk(clock_1_out), .Q(B1), .preset(MSB), .reset(or_1_out));  // open: Qn
  D_Flip_Flop d_ff_2 (.D(Output_bus_1[2]), .clk(clock_1_out), .Q(B2), .preset(TSB), .reset(or_2_out));  // open: Qn
  D_Flip_Flop d_ff_3 (.D(Output_bus_1[1]), .clk(clock_1_out), .Q(B3), .preset(SSB), .reset(or_3_out));  // open: Qn
  D_Flip_Flop d_ff_4 (.D(Output_bus_1[0]), .clk(clock_1_out), .Q(B4), .preset(LSB), .reset(or_4_out));  // open: Qn
  or or_1 (or_1_out, RST, and_1_out);
  and and_1 (and_1_out, SET, ~MSB);  // AND_Gate
  or or_2 (or_2_out, RST, and_2_out);
  and and_2 (and_2_out, SET, ~TSB);  // AND_Gate
  or or_3 (or_3_out, RST, and_3_out);
  and and_3 (and_3_out, SET, ~SSB);  // AND_Gate
  or or_4 (or_4_out, RST, and_4_out);
  and and_4 (and_4_out, SET, ~LSB);  // AND_Gate
  and and_5 (LSB, Binary_Entrance[0], SET);
  and and_6 (SSB, Binary_Entrance[1], SET);
  and and_7 (TSB, Binary_Entrance[2], SET);
  and and_8 (MSB, Binary_Entrance[3], SET);
  not not_1 (not_1_out, CLICK);
  not not_2 (not_2_out, FIN);
  not not_3 (not_3_out, B1);
  not not_4 (not_4_out, B2);
  not not_5 (not_5_out, B3);
  not not_6 (not_6_out, B4);
  and and_9 (Output_bus_1[3], not_1_out, not_2_out, B1);
  and and_10 (and_10_out, not_1_out, not_2_out, B2);
  and and_11 (and_11_out, not_2_out, not_3_out, B2, not_5_out, B4);
  and and_12 (and_12_out, CLICK, not_2_out, not_3_out, not_4_out, not_5_out, not_6_out);
  and and_13 (and_13_out, not_1_out, not_2_out, B3);
  and and_14 (and_14_out, not_2_out, not_3_out, not_4_out, B3, B4);
  and and_15 (and_15_out, CLICK, not_2_out, not_3_out, B2, not_5_out, not_6_out);
  and and_16 (and_16_out, not_1_out, not_2_out, B4);
  and and_17 (and_17_out, CLICK, not_2_out, not_3_out, not_4_out, not_6_out);
  and and_18 (and_18_out, CLICK, not_2_out, not_3_out, not_5_out, not_6_out);
  and and_19 (RETENUE, CLICK, not_2_out, not_3_out, not_4_out, not_5_out, not_6_out);
  or or_5 (Output_bus_1[2], and_10_out, and_11_out, and_12_out);
  or or_6 (Output_bus_1[1], and_13_out, and_14_out, and_15_out);
  or or_7 (Output_bus_1[0], and_16_out, and_17_out, and_18_out);

  // Other names for the same wires on the sheet: Binary[3:0] = Binary_Entrance; D4 = Output_bus_1[0];
  //   D3 = Output_bus_1[1]; D2 = Output_bus_1[2]; D1 = Output_bus_1[3]
endmodule

module Trans_Min (
  input  Enter,
  input  A,
  input  RST_AS,
  input  RST_On,
  output On_Off,
  output Start
);

  wire A_t, and_3_out, and_4_out, and_5_out, and_6_out, and_7_out, and_8_out, and_9_out, and_10_out, B1, B2,
       B3, CLICK, clock_1_out, clock_2_out, clock_3_out, clock_4_out, clock_5_out, D1, d_ff_4_q, d_ff_4_qn,
       d_ff_5_q, d_ff_5_qn, d_ff_6_q, d_ff_7_q, not_1_out, not_2_out, not_3_out, not_4_out, not_5_out;

  Clock clock_1 (.out(clock_1_out));
  Clock clock_2 (.out(clock_2_out));
  D_Flip_Flop d_ff_1 (.D(D1), .clk(clock_3_out), .Q(B1), .reset(RST_On));  // open: Qn, preset
  Clock clock_3 (.out(clock_3_out));
  D_Flip_Flop d_ff_2 (.D(Start), .clk(clock_4_out), .Q(B2), .reset(RST_AS));  // open: Qn, preset
  Clock clock_4 (.out(clock_4_out));
  D_Flip_Flop d_ff_3 (.D(On_Off), .clk(clock_5_out), .Q(B3), .reset(RST_On));  // open: Qn, preset
  Clock clock_5 (.out(clock_5_out));
  D_Flip_Flop #(.trigger("falling")) d_ff_4 (
    .D(Enter), .clk(clock_1_out), .Q(d_ff_4_q), .Qn(d_ff_4_qn));  // open: preset, reset
  D_Flip_Flop #(.trigger("falling")) d_ff_5 (
    .D(A), .clk(clock_2_out), .Q(d_ff_5_q), .Qn(d_ff_5_qn));  // open: preset, reset
  D_Flip_Flop d_ff_6 (.D(d_ff_4_qn), .clk(clock_1_out), .Q(d_ff_6_q));  // open: Qn, preset, reset
  D_Flip_Flop d_ff_7 (.D(d_ff_5_qn), .clk(clock_2_out), .Q(d_ff_7_q));  // open: Qn, preset, reset
  and and_1 (CLICK, d_ff_4_q, d_ff_6_q);
  and and_2 (A_t, d_ff_5_q, d_ff_7_q);
  not not_1 (not_1_out, CLICK);
  not not_2 (not_2_out, A_t);
  not not_3 (not_3_out, B1);
  not not_4 (not_4_out, B2);
  not not_5 (not_5_out, B3);
  and and_3 (and_3_out, not_1_out, B1);
  and and_4 (and_4_out, CLICK, not_3_out);
  and and_5 (and_5_out, not_1_out, not_2_out, B2, B3);
  and and_6 (and_6_out, not_1_out, A_t, not_4_out, B3);
  and and_7 (and_7_out, CLICK, not_2_out, B2, not_5_out);
  and and_8 (and_8_out, CLICK, A_t, not_4_out, not_5_out);
  and and_9 (and_9_out, not_1_out, B3);
  and and_10 (and_10_out, CLICK, not_5_out);
  or or_1 (D1, and_3_out, and_4_out);
  or or_2 (Start, and_5_out, and_6_out, and_7_out, and_8_out);
  or or_3 (On_Off, and_9_out, and_10_out);

  // Other names for the same wires on the sheet: D2 = Start; D3 = On_Off; RST = RST_AS; RST_1 = RST_On
endmodule

module Sonnerie (
  input  CLICK,
  input  CONDITION,
  input  RST,
  output S
);

  wire A1, and_1_out, and_2_out, and_3_out, clock_1_out, not_1_out, not_2_out, not_3_out;

  D_Flip_Flop d_ff_1 (.D(S), .clk(clock_1_out), .Q(A1), .reset(RST));  // open: Qn, preset
  Clock clock_1 (.out(clock_1_out));
  not not_1 (not_1_out, CLICK);
  not not_2 (not_2_out, CONDITION);
  not not_3 (not_3_out, A1);
  and and_1 (and_1_out, not_1_out, A1);
  and and_2 (and_2_out, not_2_out, A1);
  and and_3 (and_3_out, CLICK, CONDITION, not_3_out);
  or or_1 (S, and_1_out, and_2_out, and_3_out);

  // Other names for the same wires on the sheet: A2 = S
endmodule

module Minuteur (
  input  ENTER,
  input  A,
  input  STOP,
  input  RST,
  input  [23:0] Binary_Entrance,
  input  Input_1,
  output [23:0] Output_bus_1,
  output On_Off,
  output Sonnerie_Min
);

  wire and_1_out, and_2_out, and_5_out, and_6_out, and_7_out, and_8_out, AS, Count_Min_5_1_retenue,
       Count_Min_5_2_retenue, Count_Min_9_1_retenue, Count_Min_9_2_retenue, Count_Min_9_One_1_retenue, ENDED,
       multiplexer_1_out, not_1_out, or_2_out, or_3_out, Retenue, RST_t, STOP_t;

  or or_1 (RST_t, RST, STOP_t);
  and and_1 (and_1_out, ~Output_bus_1[23], ~Output_bus_1[22], ~Output_bus_1[21], ~Output_bus_1[20]);  // AND_Gate
  and and_2 (and_2_out, ~Output_bus_1[19], ~Output_bus_1[18], ~Output_bus_1[17], ~Output_bus_1[16]);  // AND_Gate
  and and_3 (STOP_t, STOP, Sonnerie_Min);
  and and_4 (ENDED, not_1_out, and_5_out);
  not not_1 (not_1_out, A);
  and and_5 (and_5_out, and_1_out, and_2_out, and_6_out, and_7_out, and_8_out, Retenue);
  and and_6 (and_6_out, ~Output_bus_1[15], ~Output_bus_1[14], ~Output_bus_1[13], ~Output_bus_1[12]);  // AND_Gate
  and and_7 (and_7_out, ~Output_bus_1[11], ~Output_bus_1[10], ~Output_bus_1[9], ~Output_bus_1[8]);  // AND_Gate
  and and_8 (and_8_out, ~Output_bus_1[7], ~Output_bus_1[6], ~Output_bus_1[5], ~Output_bus_1[4]);  // AND_Gate
  or or_2 (or_2_out, RST_t, ENDED);
  or or_3 (or_3_out, STOP_t, RST_t);
  Trans_Min Trans_Min_1 (.Enter(ENTER), .A(A), .RST_AS(or_2_out), .RST_On(or_3_out), .On_Off(On_Off), .Start(AS));
  Sonnerie Sonnerie_1 (.CLICK(ENDED), .CONDITION(On_Off), .RST(RST_t), .S(Sonnerie_Min));
  Multiplexer multiplexer_1 (.in0(1'b0), .in1(Input_1), .out(multiplexer_1_out), .sel(AS));
  Count_Min_9_One Count_Min_9_One_1 (
    .CLICK(multiplexer_1_out), .SET(ENTER), .RST(RST_t), .Binary_Entrance(Binary_Entrance[23:20]),
    .RETENUE(Count_Min_9_One_1_retenue), .RETENUE_END(Retenue), .S(Output_bus_1[3:0]));  // open: FIN
  Count_Min_5 Count_Min_5_1 (
    .CLICK(Count_Min_9_One_1_retenue), .SET(ENTER), .RST(RST_t), .Binary_Entrance(Binary_Entrance[19:16]),
    .RETENUE(Count_Min_5_1_retenue), .Output_bus_1(Output_bus_1[7:4]));  // open: FIN
  Count_Min_9 Count_Min_9_1 (
    .CLICK(Count_Min_5_1_retenue), .SET(ENTER), .RST(RST_t), .Binary_Entrance(Binary_Entrance[15:12]),
    .RETENUE(Count_Min_9_1_retenue), .S(Output_bus_1[11:8]));  // open: FIN
  Count_Min_5 Count_Min_5_2 (
    .CLICK(Count_Min_9_1_retenue), .SET(ENTER), .RST(RST_t), .Binary_Entrance(Binary_Entrance[11:8]),
    .RETENUE(Count_Min_5_2_retenue), .Output_bus_1(Output_bus_1[15:12]));  // open: FIN
  Count_Min_9 Count_Min_9_2 (
    .CLICK(Count_Min_5_2_retenue), .SET(ENTER), .RST(RST_t), .Binary_Entrance(Binary_Entrance[7:4]),
    .RETENUE(Count_Min_9_2_retenue), .S(Output_bus_1[19:16]));  // open: FIN
  Count_Min_5 Count_Min_5_3 (
    .CLICK(Count_Min_9_2_retenue), .SET(ENTER), .RST(RST_t), .Binary_Entrance(Binary_Entrance[3:0]),
    .Output_bus_1(Output_bus_1[23:20]));  // open: FIN, RETENUE

  // Other names for the same wires on the sheet: B5[3:0] = Binary_Entrance[3:0]; B4[3:0] = Binary_Entrance[7:4];
  //   B3[3:0] = Binary_Entrance[11:8]; B2[3:0] = Binary_Entrance[15:12]; B1[3:0] = Binary_Entrance[19:16];
  //   B0[3:0] = Binary_Entrance[23:20]; CLOCK = Input_1; S_2[3:0] = Output_bus_1[3:0]; S_1[3:0] = Output_bus_1[7:4];
  //   M_2[3:0] = Output_bus_1[11:8]; M_1[3:0] = Output_bus_1[15:12]; H_2[3:0] = Output_bus_1[19:16];
  //   H_1[3:0] = Output_bus_1[23:20]; SET = ENTER; SONNERIE_1 = Sonnerie_Min
endmodule

module Harry_Song (
  input  ONOFF,
  input  RESET,
  output V
);

  wire and_1_out, BPM_out, clock_1_out, clock_2_out, clock_3_out, clock_4_out, clock_5_out, clock_6_out,
       clock_7_out, clock_8_out, clock_9_out, clock_10_out, clock_11_out, d_ff_2_q, d_ff_5_q, d_ff_6_q,
       d_ff_7_q, d_ff_10_q, d_ff_11_q, d_ff_13_q, d_ff_14_q, d_ff_15_q, d_ff_16_q, d_ff_17_q, d_ff_19_q,
       d_ff_20_q, d_ff_21_q, d_ff_22_q, d_ff_24_q, d_ff_25_q, d_ff_26_q, d_ff_29_q, d_ff_32_q, d_ff_35_q,
       d_ff_40_q, d_ff_42_q, d_ff_43_q, d_ff_44_q, d_ff_45_q, d_ff_46_q, d_ff_47_q, d_ff_48_q, d_ff_49_q,
       d_ff_50_q, d_ff_51_q, d_ff_52_q, d_ff_53_q, d_ff_54_q, d_ff_55_q, d_ff_56_q, d_ff_57_q, d_ff_59_q,
       d_ff_62_q, d_ff_64_q, Do_m_1, Do_m_2, Do_m_3, Fa_M, La_m_1, La_m_2, La_m_3, La_m_4, La_m_5, Mi_M_1,
       Mi_m_1_t, Mi_M_2, Mi_m_2_t, Mi_m_3, multiplexer_1_out, multiplexer_2_out, multiplexer_3_out,
       multiplexer_4_out, multiplexer_5_out, multiplexer_6_out, multiplexer_7_out, multiplexer_8_out,
       multiplexer_9_out, multiplexer_10_out, multiplexer_11_out, multiplexer_12_out, not_1_out, or_1_out,
       or_2_out, or_3_out, or_4_out, or_5_out, Re, Si_b, Si_m_1, Si_m_2, Si_m_3, Si_m_4, Sol_b_M, Sol_d,
       Sol_M;

  Clock #(.highDuration(3200), .lowDuration(3200)) BPM (.out(BPM_out));
  Multiplexer multiplexer_1 (.in0(1'b0), .in1(BPM_out), .out(multiplexer_1_out), .sel(and_1_out));
  and and_1 (and_1_out, ONOFF, not_1_out);
  not not_1 (not_1_out, RESET);
  D_Flip_Flop d_ff_1 (.D(d_ff_64_q), .clk(multiplexer_1_out), .Q(Mi_m_1_t), .reset(RESET));  // open: Qn, preset
  D_Flip_Flop d_ff_2 (.D(d_ff_49_q), .clk(multiplexer_1_out), .Q(d_ff_2_q), .reset(RESET));  // open: Qn, preset
  D_Flip_Flop d_ff_3 (.D(d_ff_50_q), .clk(multiplexer_1_out), .Q(La_m_2), .reset(RESET));  // open: Qn, preset
  D_Flip_Flop d_ff_4 (.D(d_ff_51_q), .clk(multiplexer_1_out), .Q(Mi_M_1), .reset(RESET));  // open: Qn, preset
  D_Flip_Flop d_ff_5 (.D(d_ff_52_q), .clk(multiplexer_1_out), .Q(d_ff_5_q), .reset(RESET));  // open: Qn, preset
  D_Flip_Flop d_ff_6 (.D(d_ff_53_q), .clk(multiplexer_1_out), .Q(d_ff_6_q), .reset(RESET));  // open: Qn, preset
  D_Flip_Flop d_ff_7 (.D(d_ff_54_q), .clk(multiplexer_1_out), .Q(d_ff_7_q), .reset(RESET));  // open: Qn, preset
  D_Flip_Flop d_ff_8 (.D(d_ff_55_q), .clk(multiplexer_1_out), .Q(Sol_d), .reset(RESET));  // open: Qn, preset
  D_Flip_Flop d_ff_9 (.D(d_ff_56_q), .clk(multiplexer_1_out), .Q(Si_b), .reset(RESET));  // open: Qn, preset
  D_Flip_Flop d_ff_10 (.D(d_ff_57_q), .clk(multiplexer_1_out), .Q(d_ff_10_q), .reset(RESET));  // open: Qn, preset
  D_Flip_Flop d_ff_11 (.D(Mi_m_3), .clk(multiplexer_1_out), .Q(d_ff_11_q), .reset(RESET));  // open: Qn, preset
  D_Flip_Flop d_ff_12 (.D(d_ff_59_q), .clk(multiplexer_1_out), .Q(Do_m_3), .reset(RESET));  // open: Qn, preset
  D_Flip_Flop d_ff_13 (.D(La_m_5), .clk(multiplexer_1_out), .Q(d_ff_13_q), .reset(RESET));  // open: Qn, preset
  D_Flip_Flop d_ff_14 (.D(Mi_M_2), .clk(multiplexer_1_out), .Q(d_ff_14_q), .reset(RESET));  // open: Qn, preset
  D_Flip_Flop d_ff_15 (.D(d_ff_62_q), .clk(multiplexer_1_out), .Q(d_ff_15_q), .reset(RESET));  // open: Qn, preset
  D_Flip_Flop d_ff_16 (.D(Fa_M), .clk(multiplexer_1_out), .Q(d_ff_16_q), .reset(RESET));  // open: Qn, preset
  D_Flip_Flop d_ff_17 (.D(Mi_m_1_t), .clk(multiplexer_1_out), .Q(d_ff_17_q), .reset(RESET));  // open: Qn, preset
  D_Flip_Flop d_ff_18 (.D(d_ff_2_q), .clk(multiplexer_1_out), .Q(Do_m_1), .reset(RESET));  // open: Qn, preset
  D_Flip_Flop d_ff_19 (.D(La_m_2), .clk(multiplexer_1_out), .Q(d_ff_19_q), .reset(RESET));  // open: Qn, preset
  D_Flip_Flop d_ff_20 (.D(Mi_M_1), .clk(multiplexer_1_out), .Q(d_ff_20_q), .reset(RESET));  // open: Qn, preset
  D_Flip_Flop d_ff_21 (.D(d_ff_5_q), .clk(multiplexer_1_out), .Q(d_ff_21_q), .reset(RESET));  // open: Qn, preset
  D_Flip_Flop d_ff_22 (.D(d_ff_6_q), .clk(multiplexer_1_out), .Q(d_ff_22_q), .reset(RESET));  // open: Qn, preset
  D_Flip_Flop d_ff_23 (.D(d_ff_7_q), .clk(multiplexer_1_out), .Q(Do_m_2), .reset(RESET));  // open: Qn, preset
  D_Flip_Flop d_ff_24 (.D(Sol_d), .clk(multiplexer_1_out), .Q(d_ff_24_q), .reset(RESET));  // open: Qn, preset
  D_Flip_Flop d_ff_25 (.D(Si_b), .clk(multiplexer_1_out), .Q(d_ff_25_q), .reset(RESET));  // open: Qn, preset
  D_Flip_Flop d_ff_26 (.D(d_ff_10_q), .clk(multiplexer_1_out), .Q(d_ff_26_q), .reset(RESET));  // open: Qn, preset
  D_Flip_Flop d_ff_27 (.D(d_ff_11_q), .clk(multiplexer_1_out), .Q(La_m_4), .reset(RESET));  // open: Qn, preset
  D_Flip_Flop d_ff_28 (.D(Do_m_3), .clk(multiplexer_1_out), .Q(Si_m_4), .reset(RESET));  // open: Qn, preset
  D_Flip_Flop d_ff_29 (.D(d_ff_13_q), .clk(multiplexer_1_out), .Q(d_ff_29_q), .reset(RESET));  // open: Qn, preset
  D_Flip_Flop d_ff_30 (.D(d_ff_14_q), .clk(multiplexer_1_out), .Q(Sol_M), .reset(RESET));  // open: Qn, preset
  D_Flip_Flop d_ff_31 (.D(d_ff_15_q), .clk(multiplexer_1_out), .Q(Sol_b_M), .reset(RESET));  // open: Qn, preset
  D_Flip_Flop d_ff_32 (.D(d_ff_16_q), .clk(multiplexer_1_out), .Q(d_ff_32_q), .reset(RESET));  // open: Qn, preset
  D_Flip_Flop d_ff_33 (.D(d_ff_17_q), .clk(multiplexer_1_out), .Q(La_m_1), .reset(RESET));  // open: Qn, preset
  D_Flip_Flop d_ff_34 (.D(Do_m_1), .clk(multiplexer_1_out), .Q(Si_m_1), .reset(RESET));  // open: Qn, preset
  D_Flip_Flop d_ff_35 (.D(d_ff_19_q), .clk(multiplexer_1_out), .Q(d_ff_35_q), .reset(RESET));  // open: Qn, preset
  D_Flip_Flop d_ff_36 (.D(d_ff_20_q), .clk(multiplexer_1_out), .Q(Re), .reset(RESET));  // open: Qn, preset
  D_Flip_Flop d_ff_37 (.D(d_ff_21_q), .clk(multiplexer_1_out), .Q(Si_m_2), .reset(RESET));  // open: Qn, preset
  D_Flip_Flop d_ff_38 (.D(d_ff_22_q), .clk(multiplexer_1_out), .Q(La_m_3), .reset(RESET));  // open: Qn, preset
  D_Flip_Flop d_ff_39 (.D(Do_m_2), .clk(multiplexer_1_out), .Q(Si_m_3), .reset(RESET));  // open: Qn, preset
  D_Flip_Flop d_ff_40 (.D(d_ff_24_q), .clk(multiplexer_1_out), .Q(d_ff_40_q), .reset(RESET));  // open: Qn, preset
  D_Flip_Flop d_ff_41 (.D(d_ff_25_q), .clk(multiplexer_1_out), .Q(Mi_m_2_t), .reset(RESET));  // open: Qn, preset
  D_Flip_Flop d_ff_42 (.D(d_ff_26_q), .clk(multiplexer_1_out), .Q(d_ff_42_q), .reset(RESET));  // open: Qn, preset
  D_Flip_Flop d_ff_43 (.D(La_m_4), .clk(multiplexer_1_out), .Q(d_ff_43_q), .reset(RESET));  // open: Qn, preset
  D_Flip_Flop d_ff_44 (.D(Si_m_4), .clk(multiplexer_1_out), .Q(d_ff_44_q), .reset(RESET));  // open: Qn, preset
  D_Flip_Flop d_ff_45 (.D(d_ff_29_q), .clk(multiplexer_1_out), .Q(d_ff_45_q), .reset(RESET));  // open: Qn, preset
  D_Flip_Flop d_ff_46 (.D(Sol_M), .clk(multiplexer_1_out), .Q(d_ff_46_q), .reset(RESET));  // open: Qn, preset
  D_Flip_Flop d_ff_47 (.D(Sol_b_M), .clk(multiplexer_1_out), .Q(d_ff_47_q), .reset(RESET));  // open: Qn, preset
  D_Flip_Flop d_ff_48 (.D(d_ff_32_q), .clk(multiplexer_1_out), .Q(d_ff_48_q), .reset(RESET));  // open: Qn, preset
  D_Flip_Flop d_ff_49 (.D(La_m_1), .clk(multiplexer_1_out), .Q(d_ff_49_q), .reset(RESET));  // open: Qn, preset
  D_Flip_Flop d_ff_50 (.D(Si_m_1), .clk(multiplexer_1_out), .Q(d_ff_50_q), .reset(RESET));  // open: Qn, preset
  D_Flip_Flop d_ff_51 (.D(d_ff_35_q), .clk(multiplexer_1_out), .Q(d_ff_51_q), .reset(RESET));  // open: Qn, preset
  D_Flip_Flop d_ff_52 (.D(Re), .clk(multiplexer_1_out), .Q(d_ff_52_q), .reset(RESET));  // open: Qn, preset
  D_Flip_Flop d_ff_53 (.D(Si_m_2), .clk(multiplexer_1_out), .Q(d_ff_53_q), .reset(RESET));  // open: Qn, preset
  D_Flip_Flop d_ff_54 (.D(La_m_3), .clk(multiplexer_1_out), .Q(d_ff_54_q), .reset(RESET));  // open: Qn, preset
  D_Flip_Flop d_ff_55 (.D(Si_m_3), .clk(multiplexer_1_out), .Q(d_ff_55_q), .reset(RESET));  // open: Qn, preset
  D_Flip_Flop d_ff_56 (.D(d_ff_40_q), .clk(multiplexer_1_out), .Q(d_ff_56_q), .reset(RESET));  // open: Qn, preset
  D_Flip_Flop d_ff_57 (.D(Mi_m_2_t), .clk(multiplexer_1_out), .Q(d_ff_57_q), .reset(RESET));  // open: Qn, preset
  D_Flip_Flop d_ff_58 (.D(d_ff_42_q), .clk(multiplexer_1_out), .Q(Mi_m_3), .reset(RESET));  // open: Qn, preset
  D_Flip_Flop d_ff_59 (.D(d_ff_43_q), .clk(multiplexer_1_out), .Q(d_ff_59_q), .reset(RESET));  // open: Qn, preset
  D_Flip_Flop d_ff_60 (.D(d_ff_44_q), .clk(multiplexer_1_out), .Q(La_m_5), .reset(RESET));  // open: Qn, preset
  D_Flip_Flop d_ff_61 (.D(d_ff_45_q), .clk(multiplexer_1_out), .Q(Mi_M_2), .reset(RESET));  // open: Qn, preset
  D_Flip_Flop d_ff_62 (.D(d_ff_46_q), .clk(multiplexer_1_out), .Q(d_ff_62_q), .reset(RESET));  // open: Qn, preset
  D_Flip_Flop d_ff_63 (.D(d_ff_47_q), .clk(multiplexer_1_out), .Q(Fa_M), .reset(RESET));  // open: Qn, preset
  D_Flip_Flop d_ff_64 (.D(d_ff_48_q), .clk(multiplexer_1_out), .Q(d_ff_64_q), .preset(RESET));  // open: Qn, reset
  Multiplexer multiplexer_2 (.in0(1'b0), .in1(clock_1_out), .out(multiplexer_2_out), .sel(or_1_out));
  Clock #(.highDuration(24), .lowDuration(24)) clock_1 (.out(clock_1_out));
  or or_1 (or_1_out, Mi_m_1_t, Mi_m_2_t, Mi_m_3);
  Multiplexer multiplexer_3 (.in0(1'b0), .in1(clock_2_out), .out(multiplexer_3_out), .sel(or_2_out));
  Clock #(.highDuration(18), .lowDuration(18)) clock_2 (.out(clock_2_out));
  or or_2 (or_2_out, La_m_1, La_m_2, La_m_3, La_m_4, La_m_5);
  Multiplexer multiplexer_4 (.in0(1'b0), .in1(clock_3_out), .out(multiplexer_4_out), .sel(or_3_out));
  Clock #(.highDuration(15), .lowDuration(15)) clock_3 (.out(clock_3_out));
  or or_3 (or_3_out, Do_m_1, Do_m_2, Do_m_3);
  Multiplexer multiplexer_5 (.in0(1'b0), .in1(clock_4_out), .out(multiplexer_5_out), .sel(or_4_out));
  Clock #(.highDuration(16), .lowDuration(16)) clock_4 (.out(clock_4_out));
  or or_4 (or_4_out, Si_m_1, Si_m_2, Si_m_3, Si_m_4);
  Clock #(.highDuration(12), .lowDuration(12)) clock_5 (.out(clock_5_out));
  or or_5 (or_5_out, Mi_M_1, Mi_M_2);
  Clock #(.highDuration(14), .lowDuration(14)) clock_6 (.out(clock_6_out));
  Clock #(.highDuration(19), .lowDuration(19)) clock_7 (.out(clock_7_out));
  Clock #(.highDuration(17), .lowDuration(17)) clock_8 (.out(clock_8_out));
  Clock #(.highDuration(10), .lowDuration(10)) clock_9 (.out(clock_9_out));
  Clock #(.highDuration(12), .lowDuration(12)) clock_10 (.out(clock_10_out));
  Multiplexer multiplexer_6 (.in0(1'b0), .in1(clock_5_out), .out(multiplexer_6_out), .sel(or_5_out));
  Multiplexer multiplexer_7 (.in0(1'b0), .in1(clock_6_out), .out(multiplexer_7_out), .sel(Re));
  Multiplexer multiplexer_8 (.in0(1'b0), .in1(clock_7_out), .out(multiplexer_8_out), .sel(Sol_d));
  Multiplexer multiplexer_9 (.in0(1'b0), .in1(clock_8_out), .out(multiplexer_9_out), .sel(Si_b));
  Multiplexer multiplexer_10 (.in0(1'b0), .in1(clock_9_out), .out(multiplexer_10_out), .sel(Sol_M));
  Multiplexer multiplexer_11 (.in0(1'b0), .in1(clock_11_out), .out(multiplexer_11_out), .sel(Sol_b_M));
  Clock #(.highDuration(11), .lowDuration(11)) clock_11 (.out(clock_11_out));
  Multiplexer multiplexer_12 (.in0(1'b0), .in1(clock_10_out), .out(multiplexer_12_out), .sel(Fa_M));
  or or_6 (V, multiplexer_2_out, multiplexer_3_out, multiplexer_4_out, multiplexer_5_out, multiplexer_6_out, multiplexer_7_out, multiplexer_8_out, multiplexer_9_out, multiplexer_10_out, multiplexer_11_out, multiplexer_12_out);

  // Notes on the sheet:
  //   659
  //   880
  //   1046
  //   987
  //   880
  //   1328
  //   1174
  //   987
  //   880
  //   1046
  //   987
  //   830
  //   932
  //   659
  //   659
  //   880
  //   1046
  //   987
  //   880
  //   1328
  //   1567
  //   1479
  //   1396
  //   Do mineur
  //   698
  //   La mineur
  //   1046
  //   Si mineur
  //   Mi mineur
  //   987
  //   Mi majeur
  //   Re
  //   Sol Dieze
  //   Si bemol
  //   Sol Majeur
  //   Sol bemol
  //   Fa majeur
  //   659
  //   1328
  //   1174
  //   830
  //   932
  //   1567
  //   1479
  //   1396
endmodule

module Lettre_a_Elise (
  input  ONOFF,
  input  RESET,
  output V
);

  wire and_1_out, BPM_out, clock_1_out, clock_2_out, clock_3_out, clock_4_out, clock_5_out, clock_6_out,
       clock_7_out, clock_8_out, clock_9_out, d_ff_4_q, d_ff_7_q, d_ff_10_q, d_ff_15_q, d_ff_20_q, d_ff_24_q,
       d_ff_30_q, d_ff_33_q, d_ff_36_q, Do_M_1, Do_m_1_t, Do_M_2, Do_M_3, La_1, La_2, La_3, Mi_M_1, Mi_m_1_t,
       Mi_M_2, Mi_m_2_t, Mi_M_3, Mi_m_3_t, Mi_M_4, Mi_M_5, Mi_M_6, multiplexer_1_out, multiplexer_2_out,
       multiplexer_3_out, multiplexer_4_out, multiplexer_5_out, multiplexer_6_out, multiplexer_7_out,
       multiplexer_8_out, multiplexer_9_out, multiplexer_10_out, not_1_out, or_1_out, or_2_out, or_3_out,
       or_4_out, or_5_out, or_6_out, or_7_out, Re_d_1, Re_d_2, Re_d_3, Re_d_4, Re_M_1, Re_M_2, Si_M_1,
       Si_M_2, Si_M_3, Si_M_4, Sol_d_1;

  Clock #(.highDuration(3200), .lowDuration(3200)) BPM (.out(BPM_out));
  and and_1 (and_1_out, ONOFF, not_1_out);
  not not_1 (not_1_out, RESET);
  Multiplexer multiplexer_1 (.in0(1'b0), .in1(BPM_out), .out(multiplexer_1_out), .sel(and_1_out));
  D_Flip_Flop d_ff_1 (.D(d_ff_20_q), .clk(multiplexer_1_out), .Q(Mi_M_6), .reset(RESET));  // open: Qn, preset
  D_Flip_Flop d_ff_2 (.D(Re_d_4), .clk(multiplexer_1_out), .Q(Mi_M_1), .reset(RESET));  // open: Qn, preset
  D_Flip_Flop d_ff_3 (.D(Si_M_1), .clk(multiplexer_1_out), .Q(Re_M_1), .reset(RESET));  // open: Qn, preset
  D_Flip_Flop d_ff_4 (.D(d_ff_30_q), .clk(multiplexer_1_out), .Q(d_ff_4_q), .reset(RESET));  // open: Qn, preset
  D_Flip_Flop d_ff_5 (.D(La_2), .clk(multiplexer_1_out), .Q(Si_M_2), .reset(RESET));  // open: Qn, preset
  D_Flip_Flop d_ff_6 (.D(Mi_m_2_t), .clk(multiplexer_1_out), .Q(Sol_d_1), .reset(RESET));  // open: Qn, preset
  D_Flip_Flop d_ff_7 (.D(d_ff_33_q), .clk(multiplexer_1_out), .Q(d_ff_7_q), .reset(RESET));  // open: Qn, preset
  D_Flip_Flop d_ff_8 (.D(Re_d_2), .clk(multiplexer_1_out), .Q(Mi_M_4), .reset(RESET));  // open: Qn, preset
  D_Flip_Flop d_ff_9 (.D(Si_M_4), .clk(multiplexer_1_out), .Q(Re_M_2), .reset(RESET));  // open: Qn, preset
  D_Flip_Flop d_ff_10 (.D(d_ff_36_q), .clk(multiplexer_1_out), .Q(d_ff_10_q), .reset(RESET));  // open: Qn, preset
  D_Flip_Flop d_ff_11 (.D(Mi_M_6), .clk(multiplexer_1_out), .Q(Re_d_4), .reset(RESET));  // open: Qn, preset
  D_Flip_Flop d_ff_12 (.D(Mi_M_1), .clk(multiplexer_1_out), .Q(Re_d_1), .reset(RESET));  // open: Qn, preset
  D_Flip_Flop d_ff_13 (.D(Re_M_1), .clk(multiplexer_1_out), .Q(Do_M_1), .reset(RESET));  // open: Qn, preset
  D_Flip_Flop d_ff_14 (.D(d_ff_4_q), .clk(multiplexer_1_out), .Q(Do_m_1_t), .reset(RESET));  // open: Qn, preset
  D_Flip_Flop d_ff_15 (.D(Si_M_2), .clk(multiplexer_1_out), .Q(d_ff_15_q), .reset(RESET));  // open: Qn, preset
  D_Flip_Flop d_ff_16 (.D(Sol_d_1), .clk(multiplexer_1_out), .Q(Si_M_3), .reset(RESET));  // open: Qn, preset
  D_Flip_Flop d_ff_17 (.D(d_ff_7_q), .clk(multiplexer_1_out), .Q(Mi_m_3_t), .reset(RESET));  // open: Qn, preset
  D_Flip_Flop d_ff_18 (.D(Mi_M_4), .clk(multiplexer_1_out), .Q(Re_d_3), .reset(RESET));  // open: Qn, preset
  D_Flip_Flop d_ff_19 (.D(Re_M_2), .clk(multiplexer_1_out), .Q(Do_M_3), .reset(RESET));  // open: Qn, preset
  D_Flip_Flop d_ff_20 (.D(d_ff_10_q), .clk(multiplexer_1_out), .Q(d_ff_20_q), .preset(RESET));  // open: Qn, reset
  D_Flip_Flop d_ff_21 (.D(Re_d_1), .clk(multiplexer_1_out), .Q(Mi_M_2), .reset(RESET));  // open: Qn, preset
  D_Flip_Flop d_ff_22 (.D(Do_M_1), .clk(multiplexer_1_out), .Q(La_1), .reset(RESET));  // open: Qn, preset
  D_Flip_Flop d_ff_23 (.D(Do_m_1_t), .clk(multiplexer_1_out), .Q(Mi_m_1_t), .reset(RESET));  // open: Qn, preset
  D_Flip_Flop d_ff_24 (.D(d_ff_15_q), .clk(multiplexer_1_out), .Q(d_ff_24_q), .reset(RESET));  // open: Qn, preset
  D_Flip_Flop d_ff_25 (.D(Si_M_3), .clk(multiplexer_1_out), .Q(Do_M_2), .reset(RESET));  // open: Qn, preset
  D_Flip_Flop d_ff_26 (.D(Mi_m_3_t), .clk(multiplexer_1_out), .Q(Mi_M_3), .reset(RESET));  // open: Qn, preset
  D_Flip_Flop d_ff_27 (.D(Re_d_3), .clk(multiplexer_1_out), .Q(Mi_M_5), .reset(RESET));  // open: Qn, preset
  D_Flip_Flop d_ff_28 (.D(Do_M_3), .clk(multiplexer_1_out), .Q(La_3), .reset(RESET));  // open: Qn, preset
  D_Flip_Flop d_ff_29 (.D(Mi_M_2), .clk(multiplexer_1_out), .Q(Si_M_1), .reset(RESET));  // open: Qn, preset
  D_Flip_Flop d_ff_30 (.D(La_1), .clk(multiplexer_1_out), .Q(d_ff_30_q), .reset(RESET));  // open: Qn, preset
  D_Flip_Flop d_ff_31 (.D(Mi_m_1_t), .clk(multiplexer_1_out), .Q(La_2), .reset(RESET));  // open: Qn, preset
  D_Flip_Flop d_ff_32 (.D(d_ff_24_q), .clk(multiplexer_1_out), .Q(Mi_m_2_t), .reset(RESET));  // open: Qn, preset
  D_Flip_Flop d_ff_33 (.D(Do_M_2), .clk(multiplexer_1_out), .Q(d_ff_33_q), .reset(RESET));  // open: Qn, preset
  D_Flip_Flop d_ff_34 (.D(Mi_M_3), .clk(multiplexer_1_out), .Q(Re_d_2), .reset(RESET));  // open: Qn, preset
  D_Flip_Flop d_ff_35 (.D(Mi_M_5), .clk(multiplexer_1_out), .Q(Si_M_4), .reset(RESET));  // open: Qn, preset
  D_Flip_Flop d_ff_36 (.D(La_3), .clk(multiplexer_1_out), .Q(d_ff_36_q), .reset(RESET));  // open: Qn, preset
  Multiplexer multiplexer_2 (.in0(1'b0), .in1(clock_1_out), .out(multiplexer_2_out), .sel(or_1_out));
  Clock #(.highDuration(24), .lowDuration(24)) clock_1 (.out(clock_1_out));
  or or_1 (or_1_out, Mi_M_1, Mi_M_2, Mi_M_3, Mi_M_4, Mi_M_5, Mi_M_6);
  Multiplexer multiplexer_3 (.in0(1'b0), .in1(clock_2_out), .out(multiplexer_3_out), .sel(or_2_out));
  Clock #(.highDuration(26), .lowDuration(26)) clock_2 (.out(clock_2_out));
  or or_2 (or_2_out, Re_d_1, Re_d_2, Re_d_3, Re_d_4);
  Multiplexer multiplexer_4 (.in0(1'b0), .in1(clock_3_out), .out(multiplexer_4_out), .sel(or_3_out));
  Clock #(.highDuration(32), .lowDuration(32)) clock_3 (.out(clock_3_out));
  or or_3 (or_3_out, Si_M_1, Si_M_2, Si_M_3, Si_M_4);
  Multiplexer multiplexer_5 (.in0(1'b0), .in1(clock_4_out), .out(multiplexer_5_out), .sel(or_4_out));
  Clock #(.highDuration(27), .lowDuration(27)) clock_4 (.out(clock_4_out));
  or or_4 (or_4_out, Re_M_1, Re_M_2);
  Multiplexer multiplexer_6 (.in0(1'b0), .in1(clock_5_out), .out(multiplexer_6_out), .sel(or_5_out));
  Clock #(.highDuration(31), .lowDuration(31)) clock_5 (.out(clock_5_out));
  or or_5 (or_5_out, Do_M_1, Do_M_2, Do_M_3);
  Multiplexer multiplexer_7 (.in0(1'b0), .in1(clock_6_out), .out(multiplexer_7_out), .sel(Do_m_1_t));
  Clock #(.highDuration(61), .lowDuration(61)) clock_6 (.out(clock_6_out));
  Clock #(.highDuration(39), .lowDuration(39)) clock_7 (.out(clock_7_out));
  Clock #(.highDuration(49), .lowDuration(49)) clock_8 (.out(clock_8_out));
  or or_6 (or_6_out, Mi_m_1_t, Mi_m_2_t, Mi_m_3_t);
  Clock #(.highDuration(36), .lowDuration(36)) clock_9 (.out(clock_9_out));
  or or_7 (or_7_out, La_1, La_2, La_3);
  Multiplexer multiplexer_8 (.in0(1'b0), .in1(clock_7_out), .out(multiplexer_8_out), .sel(Sol_d_1));
  Multiplexer multiplexer_9 (.in0(1'b0), .in1(clock_8_out), .out(multiplexer_9_out), .sel(or_6_out));
  Multiplexer multiplexer_10 (.in0(1'b0), .in1(clock_9_out), .out(multiplexer_10_out), .sel(or_7_out));
  or or_8 (V, multiplexer_2_out, multiplexer_3_out, multiplexer_4_out, multiplexer_5_out, multiplexer_6_out, multiplexer_7_out, multiplexer_8_out, multiplexer_9_out, multiplexer_10_out);
endmodule

module Traitement (
  input  Input_1,
  output Output_1
);

  wire clock_1_out, clock_2_out, d_ff_1_qn, d_ff_2_q, d_ff_3_q, d_ff_4_q;

  Clock clock_1 (.out(clock_1_out));
  Clock clock_2 (.out(clock_2_out));
  D_Flip_Flop d_ff_1 (.D(1'b1), .clk(clock_1_out), .Qn(d_ff_1_qn));  // open: Q, preset, reset
  D_Flip_Flop d_ff_2 (.D(Input_1), .clk(clock_2_out), .Q(d_ff_2_q), .reset(d_ff_1_qn));  // open: Qn, preset
  D_Flip_Flop d_ff_3 (.D(d_ff_2_q), .clk(clock_2_out), .Q(d_ff_3_q), .reset(d_ff_1_qn));  // open: Qn, preset
  D_Flip_Flop d_ff_4 (.D(d_ff_3_q), .clk(clock_2_out), .Q(d_ff_4_q), .reset(d_ff_1_qn));  // open: Qn, preset
  and and_1 (Output_1, d_ff_2_q, d_ff_3_q, d_ff_4_q);

  // Notes on the sheet:
  //   Input_1: pull=down
  //   Output_1: pull=down
endmodule

module Decodeur (
  input  A0,
  input  B0,
  output Dir,
  output Cnt_en
);

  wire and_1_out, and_2_out, and_3_out, and_4_out, and_5_out, and_6_out, clock_1_out, d_ff_1_q, d_ff_2_q,
       not_1_out, not_2_out, not_3_out, not_4_out, or_1_out, Traitement_1_output_1, Traitement_2_output_1;

  Traitement Traitement_1 (.Input_1(A0), .Output_1(Traitement_1_output_1));
  Traitement Traitement_2 (.Input_1(B0), .Output_1(Traitement_2_output_1));
  Clock clock_1 (.out(clock_1_out));
  D_Flip_Flop d_ff_1 (.D(Traitement_2_output_1), .clk(clock_1_out), .Q(d_ff_1_q));  // open: Qn, preset, reset
  D_Flip_Flop d_ff_2 (.D(Traitement_1_output_1), .clk(clock_1_out), .Q(d_ff_2_q));  // open: Qn, preset, reset
  not not_1 (not_1_out, Traitement_1_output_1);
  not not_2 (not_2_out, Traitement_2_output_1);
  not not_3 (not_3_out, d_ff_2_q);
  not not_4 (not_4_out, d_ff_1_q);
  and and_1 (and_1_out, not_2_out, d_ff_2_q);
  and and_2 (and_2_out, Traitement_2_output_1, not_3_out);
  and and_3 (and_3_out, not_1_out, not_2_out, not_3_out, d_ff_1_q);
  and and_4 (and_4_out, not_1_out, not_2_out, d_ff_2_q, not_4_out);
  and and_5 (and_5_out, Traitement_1_output_1, Traitement_2_output_1, not_3_out, d_ff_1_q);
  and and_6 (and_6_out, Traitement_1_output_1, Traitement_2_output_1, d_ff_2_q, not_4_out);
  or or_1 (or_1_out, and_1_out, and_2_out);
  or or_2 (Cnt_en, and_3_out, and_4_out, and_5_out, and_6_out);
  LED LED_1 (.in(Dir));
  not not_5 (Dir, or_1_out);
  LED LED_2 (.in(Cnt_en));

  // Notes on the sheet:
  //   A0: pull=down
  //   B0: pull=down
  //   Dir: pull=down
  //   Cnt_en: pull=down
endmodule
module Count_Up_Down (
  input  LEFT,
  input  RIGHT,
  input  RST,
  output [2:0] Output_bus_1
);

  wire and_3_out, and_4_out, and_5_out, and_6_out, and_7_out, and_8_out, and_9_out, and_10_out, and_11_out,
       and_12_out, and_13_out, and_14_out, and_15_out, and_16_out, C0, C1, C2, clock_1_out, clock_2_out,
       clock_3_out, d_ff_1_q, d_ff_1_qn, d_ff_2_q, d_ff_2_qn, d_ff_3_q, d_ff_4_q, LEFT_t, not_1_out,
       not_2_out, not_3_out, not_4_out, not_5_out, RIGHT_t;

  D_Flip_Flop #(.trigger("falling")) d_ff_1 (
    .D(LEFT), .clk(clock_1_out), .Q(d_ff_1_q), .Qn(d_ff_1_qn));  // open: preset, reset
  Clock clock_1 (.out(clock_1_out));
  D_Flip_Flop #(.trigger("falling")) d_ff_2 (
    .D(RIGHT), .clk(clock_2_out), .Q(d_ff_2_q), .Qn(d_ff_2_qn));  // open: preset, reset
  Clock clock_2 (.out(clock_2_out));
  Clock clock_3 (.out(clock_3_out));
  D_Flip_Flop d_ff_3 (.D(d_ff_1_qn), .clk(clock_1_out), .Q(d_ff_3_q));  // open: Qn, preset, reset
  D_Flip_Flop d_ff_4 (.D(d_ff_2_qn), .clk(clock_2_out), .Q(d_ff_4_q));  // open: Qn, preset, reset
  D_Flip_Flop d_ff_5 (.D(Output_bus_1[2]), .clk(clock_3_out), .Q(C2), .reset(RST));  // open: Qn, preset
  D_Flip_Flop d_ff_6 (.D(Output_bus_1[1]), .clk(clock_3_out), .Q(C1), .reset(RST));  // open: Qn, preset
  D_Flip_Flop d_ff_7 (.D(Output_bus_1[0]), .clk(clock_3_out), .Q(C0), .reset(RST));  // open: Qn, preset
  and and_1 (LEFT_t, d_ff_1_q, d_ff_3_q);
  and and_2 (RIGHT_t, d_ff_2_q, d_ff_4_q);
  not not_1 (not_1_out, LEFT_t);
  not not_2 (not_2_out, RIGHT_t);
  not not_3 (not_3_out, C2);
  not not_4 (not_4_out, C1);
  not not_5 (not_5_out, C0);
  and and_3 (and_3_out, not_1_out, not_2_out, C2, not_4_out, not_5_out);
  and and_4 (and_4_out, not_1_out, RIGHT_t, not_3_out, C1, C0);
  and and_5 (and_5_out, LEFT_t, not_2_out, not_3_out, not_4_out, not_5_out);
  and and_6 (and_6_out, LEFT_t, RIGHT_t, C2, not_4_out, not_5_out);
  and and_7 (and_7_out, not_1_out, not_2_out, not_3_out, C1);
  and and_8 (and_8_out, not_1_out, RIGHT_t, not_3_out, not_4_out, C0);
  and and_9 (and_9_out, RIGHT_t, not_3_out, C1, not_5_out);
  and and_10 (and_10_out, LEFT_t, not_3_out, C1, C0);
  and and_11 (and_11_out, LEFT_t, not_2_out, C2, not_4_out, not_5_out);
  and and_12 (and_12_out, not_1_out, not_2_out, not_3_out, C0);
  and and_13 (and_13_out, not_1_out, RIGHT_t, not_3_out, not_5_out);
  and and_14 (and_14_out, LEFT_t, not_2_out, not_3_out, C1, not_5_out);
  and and_15 (and_15_out, LEFT_t, not_2_out, C2, not_4_out, not_5_out);
  and and_16 (and_16_out, LEFT_t, RIGHT_t, not_3_out, C0);
  or or_1 (Output_bus_1[2], and_3_out, and_4_out, and_5_out, and_6_out);
  or or_2 (Output_bus_1[1], and_7_out, and_8_out, and_9_out, and_10_out, and_11_out);
  or or_3 (Output_bus_1[0], and_12_out, and_13_out, and_14_out, and_15_out, and_16_out);

  // Other names for the same wires on the sheet: D0 = Output_bus_1[0]; D1 = Output_bus_1[1]; D2 = Output_bus_1[2]
endmodule

module Trans_Encodeur (
  input  cdir,
  input  c1,
  input  c0,
  input  i1,
  input  i0,
  output i1_out,
  output i0_out,
  output UpDown,
  output G5
);

  wire and_1_out, and_2_out, and_3_out, and_4_out, and_5_out, and_6_out, and_7_out, and_8_out, and_9_out,
       and_10_out, and_11_out, and_12_out, not_1_out, not_2_out, not_3_out, not_4_out;

  not not_1 (not_1_out, c1);
  not not_2 (not_2_out, c0);
  not not_3 (not_3_out, i1);
  not not_4 (not_4_out, i0);
  and and_1 (and_1_out, not_1_out, not_2_out, i1, not_4_out);
  and and_2 (and_2_out, not_1_out, c0, not_3_out, not_4_out);
  and and_3 (and_3_out, c1, not_2_out, i1, i0);
  and and_4 (and_4_out, c1, c0, not_3_out, i0);
  and and_5 (and_5_out, cdir, not_1_out, not_4_out);
  and and_6 (and_6_out, cdir, not_2_out, i1);
  and and_7 (and_7_out, cdir, c0, not_3_out);
  and and_8 (and_8_out, cdir, c1, i0);
  and and_9 (and_9_out, not_1_out, c0, not_3_out, not_4_out);
  and and_10 (and_10_out, not_1_out, c0, i1, i0);
  and and_11 (and_11_out, c1, not_2_out, not_3_out, not_4_out);
  and and_12 (and_12_out, c1, not_2_out, i1, i0);
  or or_1 (G5, and_9_out, and_10_out, and_11_out, and_12_out);
  or or_2 (UpDown, and_1_out, and_2_out, and_3_out, and_4_out, and_5_out, and_6_out, and_7_out, and_8_out);

  assign i0_out = i0;
  assign i1_out = i1;
endmodule

module Encodeur (
  input  CHA,
  input  CHB,
  output UpDown,
  output G5
);

  wire clock_1_out, d_ff_1_q, d_ff_2_q, Trans_Encodeur_1_i0_out, Trans_Encodeur_1_i1_out,
       Trans_Encodeur_1_updown;

  Clock clock_1 (.out(clock_1_out));
  D_Flip_Flop d_ff_1 (
    .D(Trans_Encodeur_1_i1_out), .clk(clock_1_out), .Q(d_ff_1_q), .preset(1'b0), .reset(1'b0));  // open: Qn
  Trans_Encodeur Trans_Encodeur_1 (
    .cdir(UpDown), .c1(d_ff_1_q), .c0(d_ff_2_q), .i1(CHA), .i0(CHB), .i1_out(Trans_Encodeur_1_i1_out),
    .i0_out(Trans_Encodeur_1_i0_out), .UpDown(Trans_Encodeur_1_updown), .G5(G5));
  D_Flip_Flop d_ff_2 (
    .D(Trans_Encodeur_1_i0_out), .clk(clock_1_out), .Q(d_ff_2_q), .preset(1'b0), .reset(1'b0));  // open: Qn
  D_Flip_Flop d_ff_3 (
    .D(Trans_Encodeur_1_updown), .clk(clock_1_out), .Q(UpDown), .preset(1'b0), .reset(1'b0));  // open: Qn
endmodule

module Switch_FSM (
  input  CLICK,
  input  RST,
  output SWITCH
);

  wire and_1_out, and_2_out, clock_1_out, Montant_1_output_1, not_1_out, not_2_out, undriven, UPC;

  D_Flip_Flop d_ff_1 (.D(SWITCH), .clk(clock_1_out), .Q(UPC), .reset(RST));  // open: Qn, preset
  Clock clock_1 (.out(clock_1_out));
  Montant Montant_1 (.Input_1(CLICK), .Input_2(undriven), .Output_1(Montant_1_output_1));
  not not_1 (not_1_out, Montant_1_output_1);
  not not_2 (not_2_out, UPC);
  and and_1 (and_1_out, not_1_out, UPC);
  and and_2 (and_2_out, Montant_1_output_1, not_2_out);
  or or_1 (SWITCH, and_1_out, and_2_out);

  // Other names for the same wires on the sheet: UPD = SWITCH
endmodule

module Convert_One (
  input  X0,
  input  X1,
  input  X2,
  input  X3,
  input  Y,
  output a,
  output b,
  output c,
  output d,
  output e,
  output f,
  output g,
  output DOT
);

  wire and_1_out, and_2_out, and_3_out, and_4_out, and_5_out, and_6_out, and_7_out, and_8_out, and_9_out,
       and_10_out, and_11_out, and_12_out, and_13_out, and_14_out, and_15_out, and_16_out, and_17_out,
       and_18_out, and_19_out, and_20_out, and_21_out, and_22_out, and_23_out, and_24_out, and_25_out,
       and_26_out, and_27_out, and_28_out, and_29_out, and_30_out, and_31_out, and_32_out, not_1_out,
       not_2_out, not_3_out, not_4_out;

  not not_1 (not_1_out, X0);
  not not_2 (not_2_out, X1);
  not not_3 (not_3_out, X2);
  not not_4 (not_4_out, X3);
  and and_1 (and_1_out, not_1_out, not_3_out);
  and and_2 (and_2_out, not_1_out, not_2_out, X3);
  and and_3 (and_3_out, not_2_out, not_3_out, X3);
  and and_4 (and_4_out, X1, not_4_out);
  and and_5 (and_5_out, X0, X2, not_4_out);
  and and_6 (and_6_out, not_1_out, not_2_out, not_4_out);
  and and_7 (and_7_out, not_2_out, not_3_out);
  and and_8 (and_8_out, not_3_out, not_4_out);
  and and_9 (and_9_out, not_1_out, X1, X3);
  and and_10 (and_10_out, X0, not_2_out, X3);
  and and_11 (and_11_out, X0, X1, not_4_out);
  and and_12 (and_12_out, not_2_out, not_3_out);
  and and_13 (and_13_out, not_3_out, X3);
  and and_14 (and_14_out, X2, not_4_out);
  and and_15 (and_15_out, X0, not_2_out);
  and and_16 (and_16_out, X0, not_3_out);
  and and_17 (and_17_out, not_1_out, not_2_out, not_3_out);
  and and_18 (and_18_out, not_2_out, X3);
  and and_19 (and_19_out, not_1_out, X1, not_4_out);
  and and_20 (and_20_out, X0, not_2_out, X2);
  and and_21 (and_21_out, X0, X1, not_3_out);
  and and_22 (and_22_out, not_1_out, not_3_out);
  and and_23 (and_23_out, not_2_out, X2, X3);
  and and_24 (and_24_out, not_1_out, X1);
  and and_25 (and_25_out, X1, not_3_out, X3);
  and and_26 (and_26_out, not_1_out, not_2_out);
  and and_27 (and_27_out, not_3_out, X3);
  and and_28 (and_28_out, not_1_out, X2, not_4_out);
  and and_29 (and_29_out, not_2_out, X2, not_4_out);
  and and_30 (and_30_out, X3, X2, not_2_out, not_1_out);
  and and_31 (and_31_out, not_4_out, X2, X1, X0);
  and and_32 (and_32_out, not_4_out, not_3_out, not_2_out);
  or or_1 (a, and_1_out, and_2_out, and_3_out, and_4_out, and_5_out);
  or or_2 (b, and_6_out, and_7_out, and_8_out, and_9_out, and_10_out, and_11_out);
  or or_3 (c, and_12_out, and_13_out, and_14_out, and_15_out, and_16_out);
  or or_4 (d, and_17_out, and_18_out, and_19_out, and_20_out, and_21_out);
  or or_5 (e, and_22_out, and_23_out, and_24_out, and_25_out);
  or or_6 (f, and_26_out, and_27_out, and_28_out, and_29_out);
  nor nor_1 (g, and_30_out, and_31_out, and_32_out);

  assign DOT = Y;
endmodule

module Convert_All (
  input  [23:0] Input_bus_1,
  output [47:0] Output_bus_1
);

  Convert_One Convert_One_1 (
    .X0(Input_bus_1[0]), .X1(Input_bus_1[1]), .X2(Input_bus_1[2]), .X3(Input_bus_1[3]), .Y(1'b0),
    .a(Output_bus_1[0]), .b(Output_bus_1[1]), .c(Output_bus_1[2]), .d(Output_bus_1[3]), .e(Output_bus_1[4]),
    .f(Output_bus_1[5]), .g(Output_bus_1[6]), .DOT(Output_bus_1[7]));
  Convert_One Convert_One_2 (
    .X0(Input_bus_1[4]), .X1(Input_bus_1[5]), .X2(Input_bus_1[6]), .X3(Input_bus_1[7]), .Y(1'b1),
    .a(Output_bus_1[8]), .b(Output_bus_1[9]), .c(Output_bus_1[10]), .d(Output_bus_1[11]),
    .e(Output_bus_1[12]), .f(Output_bus_1[13]), .g(Output_bus_1[14]), .DOT(Output_bus_1[15]));
  Convert_One Convert_One_3 (
    .X0(Input_bus_1[8]), .X1(Input_bus_1[9]), .X2(Input_bus_1[10]), .X3(Input_bus_1[11]), .Y(1'b0),
    .a(Output_bus_1[16]), .b(Output_bus_1[17]), .c(Output_bus_1[18]), .d(Output_bus_1[19]),
    .e(Output_bus_1[20]), .f(Output_bus_1[21]), .g(Output_bus_1[22]), .DOT(Output_bus_1[23]));
  Convert_One Convert_One_4 (
    .X0(Input_bus_1[12]), .X1(Input_bus_1[13]), .X2(Input_bus_1[14]), .X3(Input_bus_1[15]), .Y(1'b1),
    .a(Output_bus_1[24]), .b(Output_bus_1[25]), .c(Output_bus_1[26]), .d(Output_bus_1[27]),
    .e(Output_bus_1[28]), .f(Output_bus_1[29]), .g(Output_bus_1[30]), .DOT(Output_bus_1[31]));
  Convert_One Convert_One_5 (
    .X0(Input_bus_1[16]), .X1(Input_bus_1[17]), .X2(Input_bus_1[18]), .X3(Input_bus_1[19]), .Y(1'b0),
    .a(Output_bus_1[32]), .b(Output_bus_1[33]), .c(Output_bus_1[34]), .d(Output_bus_1[35]),
    .e(Output_bus_1[36]), .f(Output_bus_1[37]), .g(Output_bus_1[38]), .DOT(Output_bus_1[39]));
  Convert_One Convert_One_6 (
    .X0(Input_bus_1[20]), .X1(Input_bus_1[21]), .X2(Input_bus_1[22]), .X3(Input_bus_1[23]), .Y(1'b1),
    .a(Output_bus_1[40]), .b(Output_bus_1[41]), .c(Output_bus_1[42]), .d(Output_bus_1[43]),
    .e(Output_bus_1[44]), .f(Output_bus_1[45]), .g(Output_bus_1[46]), .DOT(Output_bus_1[47]));
endmodule

module affichage_inverse_1 (
  input  [47:0] Input_bus_1,
  output [47:0] Output_bus_1
);

  affichage_inverse_2 affichage_inverse_2_1 (
    .a1(Input_bus_1[0]), .b1(Input_bus_1[1]), .c1(Input_bus_1[2]), .d1(Input_bus_1[3]), .e1(Input_bus_1[4]),
    .f1(Input_bus_1[5]), .g1(Input_bus_1[6]), .dot1(Input_bus_1[7]), .a2(Output_bus_1[40]),
    .b2(Output_bus_1[41]), .c2(Output_bus_1[42]), .d2(Output_bus_1[43]), .e2(Output_bus_1[44]),
    .f2(Output_bus_1[45]), .g2(Output_bus_1[46]), .dot2(Output_bus_1[47]));
  affichage_inverse_2 affichage_inverse_2_2 (
    .a1(Input_bus_1[8]), .b1(Input_bus_1[9]), .c1(Input_bus_1[10]), .d1(Input_bus_1[11]),
    .e1(Input_bus_1[12]), .f1(Input_bus_1[13]), .g1(Input_bus_1[14]), .dot1(Input_bus_1[15]),
    .a2(Output_bus_1[32]), .b2(Output_bus_1[33]), .c2(Output_bus_1[34]), .d2(Output_bus_1[35]),
    .e2(Output_bus_1[36]), .f2(Output_bus_1[37]), .g2(Output_bus_1[38]), .dot2(Output_bus_1[39]));
  affichage_inverse_2 affichage_inverse_2_3 (
    .a1(Input_bus_1[16]), .b1(Input_bus_1[17]), .c1(Input_bus_1[18]), .d1(Input_bus_1[19]),
    .e1(Input_bus_1[20]), .f1(Input_bus_1[21]), .g1(Input_bus_1[22]), .dot1(Input_bus_1[23]),
    .a2(Output_bus_1[24]), .b2(Output_bus_1[25]), .c2(Output_bus_1[26]), .d2(Output_bus_1[27]),
    .e2(Output_bus_1[28]), .f2(Output_bus_1[29]), .g2(Output_bus_1[30]), .dot2(Output_bus_1[31]));
  affichage_inverse_2 affichage_inverse_2_4 (
    .a1(Input_bus_1[24]), .b1(Input_bus_1[25]), .c1(Input_bus_1[26]), .d1(Input_bus_1[27]),
    .e1(Input_bus_1[28]), .f1(Input_bus_1[29]), .g1(Input_bus_1[30]), .dot1(Input_bus_1[31]),
    .a2(Output_bus_1[16]), .b2(Output_bus_1[17]), .c2(Output_bus_1[18]), .d2(Output_bus_1[19]),
    .e2(Output_bus_1[20]), .f2(Output_bus_1[21]), .g2(Output_bus_1[22]), .dot2(Output_bus_1[23]));
  affichage_inverse_2 affichage_inverse_2_5 (
    .a1(Input_bus_1[32]), .b1(Input_bus_1[33]), .c1(Input_bus_1[34]), .d1(Input_bus_1[35]),
    .e1(Input_bus_1[36]), .f1(Input_bus_1[37]), .g1(Input_bus_1[38]), .dot1(Input_bus_1[39]),
    .a2(Output_bus_1[8]), .b2(Output_bus_1[9]), .c2(Output_bus_1[10]), .d2(Output_bus_1[11]),
    .e2(Output_bus_1[12]), .f2(Output_bus_1[13]), .g2(Output_bus_1[14]), .dot2(Output_bus_1[15]));
  affichage_inverse_2 affichage_inverse_2_6 (
    .a1(Input_bus_1[40]), .b1(Input_bus_1[41]), .c1(Input_bus_1[42]), .d1(Input_bus_1[43]),
    .e1(Input_bus_1[44]), .f1(Input_bus_1[45]), .g1(Input_bus_1[46]), .a2(Output_bus_1[0]),
    .b2(Output_bus_1[1]), .c2(Output_bus_1[2]), .d2(Output_bus_1[3]), .e2(Output_bus_1[4]),
    .f2(Output_bus_1[5]), .g2(Output_bus_1[6]), .dot2(Output_bus_1[7]));  // open: dot1
endmodule

module affichage_inverse_2 (
  input  a1,
  input  b1,
  input  c1,
  input  d1,
  input  e1,
  input  f1,
  input  g1,
  input  dot1,
  output a2,
  output b2,
  output c2,
  output d2,
  output e2,
  output f2,
  output g2,
  output dot2
);

  not not_1 (dot2, dot1);

  assign a2 = d1;
  assign b2 = e1;
  assign c2 = f1;
  assign d2 = a1;
  assign e2 = b1;
  assign f2 = c1;
  assign g2 = g1;

  // Notes on the sheet:
  //   e
endmodule

module HELLO (
  output [47:0] Output_bus_1
);


  assign Output_bus_1 = 48'h3f38387976;
endmodule

module BLACK (
  output [47:0] Output_bus_1
);


  assign Output_bus_1 = {48{1'b0}};
endmodule

module Trans_HELLO (
  input  Input_1,
  input  Input_2,
  output [47:0] Output_bus_1,
  output Output_1
);

  wire and_1_out, clock_1_out, d_ff_1_q, d_ff_2_q, d_ff_3_q, d_ff_4_q;
  wire [47:0] BLACK_1_output_bus_1, HELLO_1_output_bus_1;

  D_Flip_Flop d_ff_1 (.D(Input_1), .clk(clock_1_out), .Q(d_ff_1_q), .reset(Input_2));  // open: Qn, preset
  Clock #(.highDuration(17000), .lowDuration(17000)) clock_1 (.out(clock_1_out));
  D_Flip_Flop d_ff_2 (.D(d_ff_1_q), .clk(clock_1_out), .Q(d_ff_2_q), .reset(Input_2));  // open: Qn, preset
  D_Flip_Flop d_ff_3 (.D(d_ff_2_q), .clk(clock_1_out), .Q(d_ff_3_q), .reset(Input_2));  // open: Qn, preset
  D_Flip_Flop d_ff_4 (.D(d_ff_3_q), .clk(clock_1_out), .Q(d_ff_4_q), .reset(Input_2));  // open: Qn, preset
  BLACK BLACK_1 (.Output_bus_1(BLACK_1_output_bus_1));
  HELLO HELLO_1 (.Output_bus_1(HELLO_1_output_bus_1));
  and and_1 (and_1_out, Input_1, ~d_ff_4_q);  // AND_Gate
  Multiplexer #(.width(48)) multiplexer_1 (
    .in0(BLACK_1_output_bus_1), .in1(HELLO_1_output_bus_1), .out(Output_bus_1), .sel(and_1_out));
  or or_1 (Output_1, and_1_out, ~Input_1);  // OR_Gate

  // Other names for the same wires on the sheet: DIP_4 = Input_1; RST = Input_2
endmodule
