// Logisim project Hour.circ as structural Verilog: 4 circuits, main circuit main
module main (
  input  Input_1,
  input  Input_2,
  output [3:0] Output_bus_1,
  output [3:0] Output_bus_2,
  output Output_1
);

  wire and_1_out, Count_1_1_output_1, not_1_out, not_2_out, not_3_out, not_4_out, or_1_out, or_2_out,
       or_3_out;

  or or_1 (or_1_out, Input_2, and_1_out);
  Count_1 Count_1_1 (.Input_1(Input_1), .Input_2(or_1_out), .Output_1(Count_1_1_output_1), .Output_bus_1(Output_bus_2));
  Count_2 Count_2_1 (
    .Input_1(Count_1_1_output_1), .Input_2(or_1_out), .Output_1(Output_1), .Output_bus_1(Output_bus_1));
  not not_1 (not_1_out, Output_bus_2[2]);
  not not_2 (not_2_out, Output_bus_1[1]);
  or or_2 (or_2_out, Output_bus_2[0], Output_bus_2[1], not_1_out, Output_bus_2[3]);
  not not_3 (not_3_out, or_2_out);
  or or_3 (or_3_out, Output_bus_1[0], not_2_out, Output_bus_1[2], Output_bus_1[3]);
  not not_4 (not_4_out, or_3_out);
  and and_1 (and_1_out, not_4_out, not_3_out);
endmodule

module Compteur (
  input  Input_1,
  input  Input_2,
  input  Input_3,
  output [3:0] Output_bus_1
);

  wire d_ff_1_qn, d_ff_2_qn, d_ff_3_qn, d_ff_4_qn, or_1_out;

  D_Flip_Flop d_ff_1 (
    .D(d_ff_1_qn), .clk(Input_1), .Q(Output_bus_1[0]), .Qn(d_ff_1_qn), .reset(or_1_out));  // open: preset
  D_Flip_Flop d_ff_2 (
    .D(d_ff_2_qn), .clk(d_ff_1_qn), .Q(Output_bus_1[1]), .Qn(d_ff_2_qn), .reset(or_1_out));  // open: preset
  or or_1 (or_1_out, Input_2, Input_3);
  D_Flip_Flop d_ff_3 (
    .D(d_ff_3_qn), .clk(d_ff_2_qn), .Q(Output_bus_1[2]), .Qn(d_ff_3_qn), .reset(or_1_out));  // open: preset
  D_Flip_Flop d_ff_4 (
    .D(d_ff_4_qn), .clk(d_ff_3_qn), .Q(Output_bus_1[3]), .Qn(d_ff_4_qn), .reset(or_1_out));  // open: preset
endmodule

module Count_1 (
  input  Input_1,
  input  Input_2,
  output Output_1,
  output [3:0] Output_bus_1
);

  wire not_1_out, not_2_out, not_3_out;

  not not_1 (not_1_out, Output_1);
  or or_1 (Output_1, Output_bus_1[0], not_2_out, Output_bus_1[2], not_3_out);
  not not_2 (not_2_out, Output_bus_1[1]);
  not not_3 (not_3_out, Output_bus_1[3]);
  Compteur compteur_1 (.Input_1(Input_1), .Input_2(Input_2), .Input_3(not_1_out), .Output_bus_1(Output_bus_1));
endmodule

module Count_2 (
  input  Input_1,
  input  Input_2,
  output Output_1,
  output [3:0] Output_bus_1
);

  wire not_1_out, not_2_out, not_3_out;

  not not_1 (not_1_out, Output_1);
  or or_1 (Output_1, Output_bus_1[0], not_2_out, not_3_out, Output_bus_1[3]);
  not not_2 (not_2_out, Output_bus_1[1]);
  not not_3 (not_3_out, Output_bus_1[2]);
  Compteur compteur_1 (.Input_1(Input_1), .Input_2(Input_2), .Input_3(not_1_out), .Output_bus_1(Output_bus_1));
endmodule
