// Logisim project Selctor.circ as structural Verilog: 1 circuit, main circuit main
module main (
  input  Input_1,
  input  Input_2,
  input  Input_3,
  input  Input_4,
  output Output_1,
  output Output_2,
  output Output_3,
  output Output_4,
  output Output_5,
  output Output_6
);

  wire and_1_out, d_ff_1_qn, d_ff_2_qn, d_ff_3_qn, d_ff_4_qn, d_ff_5_qn, not_1_out, not_2_out, not_3_out,
       not_4_out, not_5_out, not_6_out, not_7_out, not_8_out, not_9_out, not_10_out, not_11_out, or_1_out,
       or_2_out, or_3_out, or_4_out, or_5_out, or_6_out, or_7_out, or_8_out, or_9_out;
  wire [3:0] d_ff_2_q;

  not not_1 (not_1_out, Input_1);
  D_Flip_Flop d_ff_1 (.D(d_ff_1_qn), .clk(Input_2), .Q(Output_6), .Qn(d_ff_1_qn), .reset(Input_4));  // open: preset
  or or_1 (or_1_out, Input_4, not_3_out);
  and and_1 (and_1_out, Output_6, not_1_out, Input_3);
  or or_2 (or_2_out, Input_4, not_3_out);
  or or_3 (or_3_out, Input_4, not_3_out);
  D_Flip_Flop d_ff_2 (
    .D(d_ff_2_qn), .clk(and_1_out), .Q(d_ff_2_q[0]), .Qn(d_ff_2_qn), .preset(or_1_out));  // open: reset
  D_Flip_Flop d_ff_3 (
    .D(d_ff_3_qn), .clk(d_ff_2_qn), .Q(d_ff_2_q[1]), .Qn(d_ff_3_qn), .reset(or_2_out));  // open: preset
  D_Flip_Flop d_ff_4 (
    .D(d_ff_4_qn), .clk(d_ff_3_qn), .Q(d_ff_2_q[2]), .Qn(d_ff_4_qn), .preset(Input_4), .reset(not_3_out));
  D_Flip_Flop d_ff_5 (
    .D(d_ff_5_qn), .clk(d_ff_4_qn), .Q(d_ff_2_q[3]), .Qn(d_ff_5_qn), .reset(or_3_out));  // open: preset
  not not_2 (not_2_out, d_ff_2_q[2]);
  not not_3 (not_3_out, or_4_out);
  not not_4 (not_4_out, d_ff_2_q[1]);
  or or_4 (or_4_out, d_ff_2_q[3], not_2_out, not_4_out, d_ff_2_q[0]);
  not not_5 (not_5_out, d_ff_2_q[0]);
  not not_6 (not_6_out, d_ff_2_q[1]);
  not not_7 (not_7_out, d_ff_2_q[0]);
  not not_8 (not_8_out, d_ff_2_q[1]);
  not not_9 (not_9_out, d_ff_2_q[2]);
  not not_10 (not_10_out, d_ff_2_q[0]);
  not not_11 (not_11_out, d_ff_2_q[2]);
  or or_5 (or_5_out, not_5_out, d_ff_2_q[1], d_ff_2_q[2], d_ff_2_q[3]);
  not not_12 (Output_1, or_5_out);
  or or_6 (or_6_out, d_ff_2_q[0], not_6_out, d_ff_2_q[2], d_ff_2_q[3]);
  not not_13 (Output_2, or_6_out);
  not not_14 (Output_3, or_7_out);
  or or_7 (or_7_out, not_7_out, not_8_out, d_ff_2_q[2], d_ff_2_q[3]);
  not not_15 (Output_4, or_8_out);
  not not_16 (Output_5, or_9_out);
  or or_8 (or_8_out, d_ff_2_q[0], d_ff_2_q[1], not_9_out, d_ff_2_q[3]);
  or or_9 (or_9_out, not_10_out, d_ff_2_q[1], not_11_out, d_ff_2_q[3]);
endmodule
